// Logisim project F3-2to4-decoder.circ as structural Verilog
module Decoder38 (
  input  in_1,
  input  in_2,
  input  in_3,
  output out_4,
  output out_5,
  output out_6,
  output out_7,
  output out_8,
  output out_9,
  output out_10,
  output out_11
);

  wire transistor_1_out;

  Transistor transistor_1 (.in(1'b1), .out(transistor_1_out), .gate(in_3));
  Transistor #(.\type ("n")) transistor_2 (.in(1'b0), .out(transistor_1_out), .gate(in_3));
  Decoder24 decoder24_1 (._1(in_1), ._2(in_2), .en(transistor_1_out), .Y0(out_4), .Y1(out_5), .Y2(out_6), .Y3(out_7));
  Decoder24 decoder24_2 (._1(in_1), ._2(in_2), .en(in_3), .Y0(out_8), .Y1(out_9), .Y2(out_10), .Y3(out_11));
endmodule

module OR2 (
  input  A,
  input  B,
  output Y
);

  wire transistor_1_out, transistor_2_out;

  Transistor transistor_1 (.in(1'b1), .out(transistor_1_out), .gate(A));
  Transistor transistor_2 (.in(transistor_1_out), .out(transistor_2_out), .gate(B));
  Transistor #(.\type ("n")) transistor_3 (.in(1'b0), .out(transistor_2_out), .gate(A));
  Transistor #(.\type ("n")) transistor_4 (.in(1'b0), .out(transistor_2_out), .gate(B));
  Transistor transistor_5 (.in(1'b1), .out(Y), .gate(transistor_2_out));
  Transistor #(.\type ("n")) transistor_6 (.in(1'b0), .out(Y), .gate(transistor_2_out));
endmodule

module Decoder24 (
  input  _1,
  input  _2,
  input  en,
  output Y0,
  output Y1,
  output Y2,
  output Y3
);

  wire transistor_1_out, transistor_3_out, transistor_5_out, transistor_6_out, transistor_7_out,
       transistor_8_out, transistor_11_out, transistor_12_out, transistor_15_out, transistor_16_out,
       transistor_19_out, transistor_20_out, transistor_21_out, transistor_26_out;

  Transistor transistor_1 (.in(1'b1), .out(transistor_1_out), .gate(_1));
  Transistor #(.\type ("n")) transistor_2 (.in(1'b0), .out(transistor_1_out), .gate(_1));
  Transistor transistor_3 (.in(1'b1), .out(transistor_3_out), .gate(_2));
  Transistor #(.\type ("n")) transistor_4 (.in(1'b0), .out(transistor_3_out), .gate(_2));
  Transistor transistor_5 (.in(1'b1), .out(transistor_5_out), .gate(transistor_1_out));
  Transistor transistor_6 (.in(1'b1), .out(transistor_6_out), .gate(_1));
  Transistor #(.\type ("n")) transistor_7 (.in(1'b0), .out(transistor_7_out), .gate(en));
  Transistor #(.\type ("n")) transistor_8 (.in(transistor_7_out), .out(transistor_8_out), .gate(transistor_1_out));
  Transistor #(.\type ("n")) transistor_9 (.in(transistor_8_out), .out(transistor_5_out), .gate(transistor_3_out));
  Transistor transistor_10 (.in(1'b1), .out(transistor_5_out), .gate(en));
  Transistor #(.\type ("n")) transistor_11 (.in(1'b0), .out(transistor_11_out), .gate(en));
  Transistor #(.\type ("n")) transistor_12 (.in(transistor_11_out), .out(transistor_12_out), .gate(_1));
  Transistor #(.\type ("n")) transistor_13 (.in(transistor_12_out), .out(transistor_6_out), .gate(transistor_3_out));
  Transistor transistor_14 (.in(1'b1), .out(transistor_6_out), .gate(en));
  Transistor #(.\type ("n")) transistor_15 (.in(transistor_26_out), .out(transistor_15_out), .gate(transistor_1_out));
  Transistor #(.\type ("n")) transistor_16 (.in(transistor_15_out), .out(transistor_16_out), .gate(_2));
  Transistor transistor_17 (.in(1'b1), .out(transistor_16_out), .gate(en));
  Transistor transistor_18 (.in(1'b1), .out(transistor_16_out), .gate(transistor_1_out));
  Transistor #(.\type ("n")) transistor_19 (.in(1'b0), .out(transistor_19_out), .gate(en));
  Transistor #(.\type ("n")) transistor_20 (.in(transistor_19_out), .out(transistor_20_out), .gate(_1));
  Transistor #(.\type ("n")) transistor_21 (.in(transistor_20_out), .out(transistor_21_out), .gate(_2));
  Transistor transistor_22 (.in(1'b1), .out(transistor_21_out), .gate(en));
  Transistor transistor_23 (.in(1'b1), .out(transistor_21_out), .gate(_1));
  Transistor transistor_24 (.in(1'b1), .out(transistor_5_out), .gate(transistor_3_out));
  Transistor transistor_25 (.in(1'b1), .out(transistor_6_out), .gate(transistor_3_out));
  Transistor #(.\type ("n")) transistor_26 (.in(1'b0), .out(transistor_26_out), .gate(en));
  Transistor transistor_27 (.in(1'b1), .out(transistor_16_out), .gate(_2));
  Transistor transistor_28 (.in(1'b1), .out(transistor_21_out), .gate(_2));
  Transistor transistor_29 (.in(1'b1), .out(Y0), .gate(transistor_5_out));
  Transistor #(.\type ("n")) transistor_30 (.in(1'b0), .out(Y0), .gate(transistor_5_out));
  Transistor transistor_31 (.in(1'b1), .out(Y1), .gate(transistor_6_out));
  Transistor #(.\type ("n")) transistor_32 (.in(1'b0), .out(Y1), .gate(transistor_6_out));
  Transistor transistor_33 (.in(1'b1), .out(Y2), .gate(transistor_16_out));
  Transistor #(.\type ("n")) transistor_34 (.in(1'b0), .out(Y2), .gate(transistor_16_out));
  Transistor transistor_35 (.in(1'b1), .out(Y3), .gate(transistor_21_out));
  Transistor #(.\type ("n")) transistor_36 (.in(1'b0), .out(Y3), .gate(transistor_21_out));
endmodule

module Decoder416 (
  input  A0,
  input  A1,
  input  A2,
  input  A3,
  output out_5,
  output out_6,
  output out_7,
  output out_8,
  output out_9,
  output out_10,
  output out_11,
  output out_12,
  output out_13,
  output out_14,
  output out_15,
  output out_16,
  output out_17,
  output out_18,
  output out_19,
  output out_20
);

  wire decoder24_1_y0, decoder24_1_y1, decoder24_1_y2, decoder24_1_y3;

  Decoder24 decoder24_1 (
    ._1(A2), ._2(A3), .en(1'b1), .Y0(decoder24_1_y0), .Y1(decoder24_1_y1), .Y2(decoder24_1_y2),
    .Y3(decoder24_1_y3));
  Decoder24 decoder24_2 (._1(A0), ._2(A1), .en(decoder24_1_y0), .Y0(out_5), .Y1(out_6), .Y2(out_7), .Y3(out_8));
  Decoder24 decoder24_3 (._1(A0), ._2(A1), .en(decoder24_1_y1), .Y0(out_9), .Y1(out_10), .Y2(out_11), .Y3(out_12));
  Decoder24 decoder24_4 (._1(A0), ._2(A1), .en(decoder24_1_y2), .Y0(out_13), .Y1(out_14), .Y2(out_15), .Y3(out_16));
  Decoder24 decoder24_5 (._1(A0), ._2(A1), .en(decoder24_1_y3), .Y0(out_17), .Y1(out_18), .Y2(out_19), .Y3(out_20));
endmodule

module Seg7 (
  input  in_1,
  input  in_2,
  input  in_3,
  input  in_4
);

  wire A_out, B_out, C_out, D_out, decoder416_1_out_5, decoder416_1_out_6, decoder416_1_out_7,
       decoder416_1_out_8, decoder416_1_out_9, decoder416_1_out_10, decoder416_1_out_11, decoder416_1_out_12,
       decoder416_1_out_13, decoder416_1_out_14, decoder416_1_out_15, decoder416_1_out_16,
       decoder416_1_out_17, decoder416_1_out_18, decoder416_1_out_19, decoder416_1_out_20, E_out, F_out,
       G_out, or_1_out;

  Decoder416 decoder416_1 (
    .A0(in_1), .A1(in_2), .A2(in_3), .A3(in_4), .out_5(decoder416_1_out_5), .out_6(decoder416_1_out_6),
    .out_7(decoder416_1_out_7), .out_8(decoder416_1_out_8), .out_9(decoder416_1_out_9),
    .out_10(decoder416_1_out_10), .out_11(decoder416_1_out_11), .out_12(decoder416_1_out_12),
    .out_13(decoder416_1_out_13), .out_14(decoder416_1_out_14), .out_15(decoder416_1_out_15),
    .out_16(decoder416_1_out_16), .out_17(decoder416_1_out_17), .out_18(decoder416_1_out_18),
    .out_19(decoder416_1_out_19), .out_20(decoder416_1_out_20));
  or or_1 (or_1_out, decoder416_1_out_15, decoder416_1_out_16, decoder416_1_out_17, decoder416_1_out_18, decoder416_1_out_19, decoder416_1_out_20);
  or D (D_out, decoder416_1_out_5, decoder416_1_out_7, decoder416_1_out_8, decoder416_1_out_10, decoder416_1_out_11, decoder416_1_out_13, decoder416_1_out_14);
  or E (E_out, decoder416_1_out_5, decoder416_1_out_7, decoder416_1_out_11, decoder416_1_out_13);
  or F (F_out, decoder416_1_out_5, decoder416_1_out_9, decoder416_1_out_10, decoder416_1_out_11, decoder416_1_out_13, decoder416_1_out_14);
  or G (G_out, decoder416_1_out_7, decoder416_1_out_8, decoder416_1_out_9, decoder416_1_out_10, decoder416_1_out_11, decoder416_1_out_13, decoder416_1_out_14);
  or B (B_out, decoder416_1_out_5, decoder416_1_out_6, decoder416_1_out_7, decoder416_1_out_8, decoder416_1_out_9, decoder416_1_out_12, decoder416_1_out_13, decoder416_1_out_14);
  or A (A_out, decoder416_1_out_5, decoder416_1_out_7, decoder416_1_out_8, decoder416_1_out_10, decoder416_1_out_11, decoder416_1_out_12, decoder416_1_out_13, decoder416_1_out_14);
  or C (C_out, decoder416_1_out_5, decoder416_1_out_6, decoder416_1_out_8, decoder416_1_out_9, decoder416_1_out_10, decoder416_1_out_11, decoder416_1_out_12, decoder416_1_out_13, decoder416_1_out_14);
  _7_Segment_Display u_7_segment_display_1 (
    .g(G_out), .f(F_out), .a(A_out), .b(B_out), .e(E_out), .d(D_out), .c(C_out), .dp(or_1_out));
endmodule

module Encoder164 (
  input  A0,
  input  A1,
  input  A2,
  input  A3,
  input  A4,
  input  A5,
  input  A6,
  input  A7,
  input  A8,
  input  A9,
  input  A10,
  input  A11,
  input  A12,
  input  A13,
  input  A14,
  input  A15,
  output out_17,
  output out_18,
  output out_19,
  output out_20
);

  or Y0 (out_17, A1, A3, A5, A7, A9, A11, A13, A15);
  or Y1 (out_18, A2, A3, A6, A7, A10, A11, A14, A15);
  or Y2 (out_19, A4, A5, A6, A7, A12, A13, A14, A15);
  or Y3 (out_20, A8, A9, A10, A11, A12, A13, A14, A15);
endmodule

module Encoder164p (
  input  A15,
  input  A14,
  input  A13,
  input  A12,
  input  A11,
  input  A10,
  input  A9,
  input  A8,
  input  A7,
  input  A6,
  input  A5,
  input  A4,
  input  A3,
  input  A2,
  input  A1,
  input  A0,
  output Y0,
  output Y1,
  output Y2,
  output Y3
);

  wire and_1_out, and_2_out, and_3_out, and_4_out, and_5_out, and_6_out, and_7_out, and_8_out, and_9_out,
       and_10_out, and_11_out, and_12_out, and_13_out, and_14_out, and_15_out, and_16_out, and_17_out,
       and_18_out, and_19_out, and_20_out, and_21_out, and_22_out, and_23_out, and_24_out, and_25_out,
       and_26_out, and_28_out, not_1_out, not_2_out, not_3_out, not_4_out, not_5_out, not_6_out, not_7_out,
       not_8_out, not_9_out, not_10_out, not_11_out, not_12_out, not_13_out, not_14_out, not_15_out;

  not not_1 (not_1_out, A15);
  not not_2 (not_2_out, A14);
  not not_3 (not_3_out, A13);
  not not_4 (not_4_out, A12);
  not not_5 (not_5_out, A11);
  not not_6 (not_6_out, A10);
  not not_7 (not_7_out, A9);
  not not_8 (not_8_out, A8);
  not not_9 (not_9_out, A7);
  not not_10 (not_10_out, A6);
  not not_11 (not_11_out, A5);
  not not_12 (not_12_out, A4);
  not not_13 (not_13_out, A3);
  not not_14 (not_14_out, A2);
  not not_15 (not_15_out, A1);
  and and_1 (and_1_out, not_1_out, not_2_out);
  and and_2 (and_2_out, not_1_out, A14);
  and and_3 (and_3_out, and_1_out, not_3_out);
  and and_4 (and_4_out, and_1_out, A13);
  and and_5 (and_5_out, and_3_out, not_4_out);
  and and_6 (and_6_out, and_3_out, A12);
  and and_7 (and_7_out, and_5_out, not_5_out);
  and and_8 (and_8_out, and_5_out, A11);
  and and_9 (and_9_out, and_7_out, not_6_out);
  and and_10 (and_10_out, and_7_out, A10);
  and and_11 (and_11_out, and_9_out, not_7_out);
  and and_12 (and_12_out, and_9_out, A9);
  and and_13 (and_13_out, and_11_out, not_8_out);
  and and_14 (and_14_out, and_11_out, A8);
  and and_15 (and_15_out, and_13_out, not_9_out);
  and and_16 (and_16_out, and_13_out, A7);
  and and_17 (and_17_out, and_15_out, not_10_out);
  and and_18 (and_18_out, and_15_out, A6);
  and and_19 (and_19_out, and_17_out, not_11_out);
  and and_20 (and_20_out, and_17_out, A5);
  and and_21 (and_21_out, and_19_out, not_12_out);
  and and_22 (and_22_out, and_19_out, A4);
  and and_23 (and_23_out, and_21_out, not_13_out);
  and and_24 (and_24_out, and_21_out, A3);
  and and_25 (and_25_out, and_23_out, not_14_out);
  and and_26 (and_26_out, and_23_out, A2);
  // AND_Gate and_27 has open pins: in0=and_25_out, in1=not_15_out, out=open
  and and_28 (and_28_out, and_25_out, A1);
  or u_Y0 (Y0, and_28_out, and_24_out, and_20_out, and_16_out, and_12_out, and_8_out, and_4_out, A15);
  or u_Y1 (Y1, and_26_out, and_24_out, and_18_out, and_16_out, and_10_out, and_8_out, and_2_out, A15);
  or u_Y2 (Y2, and_22_out, and_20_out, and_18_out, and_16_out, and_6_out, and_4_out, and_2_out, A15);
  or u_Y3 (Y3, and_14_out, and_12_out, and_10_out, and_8_out, and_6_out, and_4_out, and_2_out, A15);
endmodule

module Multiplexer121 (
  input  in_1,
  input  in_2,
  input  in_3,
  output out_4
);

  wire and_1_out, and_2_out, decoder12_1_out_2, decoder12_1_out_3;

  Decoder12 decoder12_1 (.in_1(in_2), .out_2(decoder12_1_out_2), .out_3(decoder12_1_out_3));
  and and_1 (and_1_out, in_1, decoder12_1_out_2);
  and and_2 (and_2_out, decoder12_1_out_3, in_3);
  or or_1 (out_4, and_1_out, and_2_out);
endmodule

module Decoder12 (
  input  in_1,
  output out_2,
  output out_3
);

  Transistor transistor_1 (.in(1'b1), .out(out_2), .gate(in_1));
  Transistor #(.\type ("n")) transistor_2 (.in(1'b0), .out(out_2), .gate(in_1));

  assign out_3 = in_1;
endmodule

module Multiplexer341 (
  input  in_1,
  input  in_2,
  input  in_3,
  input  in_4,
  input  in_5,
  input  in_6,
  input  in_7,
  input  in_8,
  input  in_9,
  input  in_10,
  input  in_11,
  input  in_12,
  input  in_13,
  input  in_14,
  output out_15,
  output out_16,
  output out_17
);

  wire and_1_out, and_2_out, and_3_out, and_4_out, and_5_out, and_6_out, and_7_out, and_8_out, and_9_out,
       and_10_out, and_11_out, and_12_out, decoder24_1_y0, decoder24_1_y1, decoder24_1_y2, decoder24_1_y3,
       decoder24_2_y0, decoder24_2_y1, decoder24_2_y2, decoder24_2_y3, decoder24_3_y0, decoder24_3_y1,
       decoder24_3_y2, decoder24_3_y3;

  Decoder24 decoder24_1 (
    ._1(in_6), ._2(in_8), .en(1'b1), .Y0(decoder24_1_y0), .Y1(decoder24_1_y1), .Y2(decoder24_1_y2),
    .Y3(decoder24_1_y3));
  Decoder24 decoder24_2 (
    ._1(in_6), ._2(in_8), .en(1'b1), .Y0(decoder24_2_y0), .Y1(decoder24_2_y1), .Y2(decoder24_2_y2),
    .Y3(decoder24_2_y3));
  Decoder24 decoder24_3 (
    ._1(in_6), ._2(in_8), .en(1'b1), .Y0(decoder24_3_y0), .Y1(decoder24_3_y1), .Y2(decoder24_3_y2),
    .Y3(decoder24_3_y3));
  and and_1 (and_1_out, decoder24_1_y0, in_1);
  and and_2 (and_2_out, decoder24_1_y1, in_2);
  and and_3 (and_3_out, in_3, decoder24_1_y2);
  and and_4 (and_4_out, in_4, decoder24_1_y3);
  and and_5 (and_5_out, decoder24_2_y0, in_5);
  and and_6 (and_6_out, decoder24_2_y1, in_7);
  and and_7 (and_7_out, in_9, decoder24_2_y2);
  and and_8 (and_8_out, in_10, decoder24_2_y3);
  and and_9 (and_9_out, decoder24_3_y0, in_11);
  and and_10 (and_10_out, decoder24_3_y1, in_12);
  and and_11 (and_11_out, in_13, decoder24_3_y2);
  and and_12 (and_12_out, in_14, decoder24_3_y3);
  or or_1 (out_15, and_1_out, and_2_out, and_3_out, and_4_out);
  or or_2 (out_16, and_5_out, and_6_out, and_7_out, and_8_out);
  or or_3 (out_17, and_9_out, and_10_out, and_11_out, and_12_out);
endmodule

module Comparator4 (
  input  in_1,
  input  in_2,
  input  in_3,
  input  in_4,
  input  in_5,
  input  in_6,
  input  in_7,
  input  in_8
);

  wire and_1_out, xnor_1_out, xnor_2_out, xnor_3_out, xnor_4_out;

  xnor xnor_1 (xnor_1_out, in_1, in_2);
  xnor xnor_2 (xnor_2_out, in_3, in_4);
  xnor xnor_3 (xnor_3_out, in_5, in_6);
  xnor xnor_4 (xnor_4_out, in_7, in_8);
  and and_1 (and_1_out, xnor_1_out, xnor_2_out, xnor_3_out, xnor_4_out);
  LED led_1 (.in(and_1_out));
endmodule

module HalfAdder (
  input  in_1,
  input  in_2,
  output S,
  output Cout
);

  xor xor_1 (S, in_1, in_2);
  and and_1 (Cout, in_1, in_2);
endmodule

module FullAdder (
  input  in_1,
  input  in_2,
  input  Cin,
  output out_4,
  output Cout
);

  wire halfadder_1_cout, halfadder_1_s, halfadder_2_cout;

  HalfAdder halfadder_1 (.in_1(in_1), .in_2(in_2), .S(halfadder_1_s), .Cout(halfadder_1_cout));
  HalfAdder halfadder_2 (.in_1(halfadder_1_s), .in_2(Cin), .S(out_4), .Cout(halfadder_2_cout));
  or or_1 (Cout, halfadder_2_cout, halfadder_1_cout);
endmodule

module BitAdder4Seg7hex (
  input  in_1,
  input  in_2,
  input  in_3,
  input  in_4,
  input  in_5,
  input  in_6,
  input  in_7,
  input  in_8,
  input  in_9
);

  wire decoder416_1_out_5, decoder416_1_out_6, decoder416_1_out_7, decoder416_1_out_8, decoder416_1_out_9,
       decoder416_1_out_10, decoder416_1_out_11, decoder416_1_out_12, decoder416_1_out_13,
       decoder416_1_out_14, decoder416_1_out_15, decoder416_1_out_16, decoder416_1_out_17,
       decoder416_1_out_18, decoder416_1_out_19, decoder416_1_out_20, fulladder_1_cout, fulladder_1_out_4,
       fulladder_2_cout, fulladder_2_out_4, fulladder_3_cout, fulladder_3_out_4, fulladder_4_cout,
       fulladder_4_out_4, ha_1_out, ha_2_out, ha_out, hb_1_out, hb_2_out, hb_out, hc_1_out, hc_2_out, hc_out,
       hd_1_out, hd_2_out, hd_out, he_1_out, he_2_out, he_out, hf_1_out, hf_2_out, hf_out, hg_1_out,
       hg_2_out, hg_out;

  FullAdder fulladder_1 (.in_1(in_1), .in_2(in_5), .Cin(in_9), .out_4(fulladder_1_out_4), .Cout(fulladder_1_cout));
  FullAdder fulladder_2 (
    .in_1(in_2), .in_2(in_6), .Cin(fulladder_1_cout), .out_4(fulladder_2_out_4), .Cout(fulladder_2_cout));
  FullAdder fulladder_3 (
    .in_1(in_3), .in_2(in_7), .Cin(fulladder_2_cout), .out_4(fulladder_3_out_4), .Cout(fulladder_3_cout));
  FullAdder fulladder_4 (
    .in_1(in_4), .in_2(in_8), .Cin(fulladder_3_cout), .out_4(fulladder_4_out_4), .Cout(fulladder_4_cout));
  LED led_1 (.in(fulladder_4_cout));
  Decoder416 decoder416_1 (
    .A0(fulladder_1_out_4), .A1(fulladder_2_out_4), .A2(fulladder_3_out_4), .A3(fulladder_4_out_4),
    .out_5(decoder416_1_out_5), .out_6(decoder416_1_out_6), .out_7(decoder416_1_out_7),
    .out_8(decoder416_1_out_8), .out_9(decoder416_1_out_9), .out_10(decoder416_1_out_10),
    .out_11(decoder416_1_out_11), .out_12(decoder416_1_out_12), .out_13(decoder416_1_out_13),
    .out_14(decoder416_1_out_14), .out_15(decoder416_1_out_15), .out_16(decoder416_1_out_16),
    .out_17(decoder416_1_out_17), .out_18(decoder416_1_out_18), .out_19(decoder416_1_out_19),
    .out_20(decoder416_1_out_20));
  or ha_1 (ha_1_out, decoder416_1_out_5, decoder416_1_out_7, decoder416_1_out_8, decoder416_1_out_10, decoder416_1_out_11, decoder416_1_out_12, decoder416_1_out_13, decoder416_1_out_14);
  or ha_2 (ha_2_out, decoder416_1_out_15, decoder416_1_out_17, decoder416_1_out_19, decoder416_1_out_20);
  or ha (ha_out, ha_1_out, ha_2_out);
  or hb_1 (hb_1_out, decoder416_1_out_5, decoder416_1_out_6, decoder416_1_out_7, decoder416_1_out_8, decoder416_1_out_9, decoder416_1_out_12, decoder416_1_out_13, decoder416_1_out_14);
  or hb_2 (hb_2_out, decoder416_1_out_15, decoder416_1_out_18, decoder416_1_out_15, decoder416_1_out_15);
  or hb (hb_out, hb_1_out, hb_2_out);
  or hc_1 (hc_1_out, decoder416_1_out_5, decoder416_1_out_6, decoder416_1_out_8, decoder416_1_out_9, decoder416_1_out_10, decoder416_1_out_11, decoder416_1_out_12, decoder416_1_out_13);
  or hc_2 (hc_2_out, decoder416_1_out_14, decoder416_1_out_15, decoder416_1_out_16, decoder416_1_out_18);
  or hc (hc_out, hc_1_out, hc_2_out);
  or hd_1 (hd_1_out, decoder416_1_out_5, decoder416_1_out_7, decoder416_1_out_8, decoder416_1_out_10, decoder416_1_out_11, decoder416_1_out_13, decoder416_1_out_14, decoder416_1_out_16);
  or hd_2 (hd_2_out, decoder416_1_out_17, decoder416_1_out_18, decoder416_1_out_19, decoder416_1_out_17);
  or hd (hd_out, hd_1_out, hd_2_out);
  or he_1 (he_1_out, decoder416_1_out_5, decoder416_1_out_7, decoder416_1_out_11, decoder416_1_out_13, decoder416_1_out_15, decoder416_1_out_16, decoder416_1_out_17, decoder416_1_out_18);
  or he_2 (he_2_out, decoder416_1_out_19, decoder416_1_out_20, decoder416_1_out_19, decoder416_1_out_19);
  or he (he_out, he_1_out, he_2_out);
  or hf_1 (hf_1_out, decoder416_1_out_5, decoder416_1_out_9, decoder416_1_out_10, decoder416_1_out_11, decoder416_1_out_13, decoder416_1_out_14, decoder416_1_out_15, decoder416_1_out_16);
  or hf_2 (hf_2_out, decoder416_1_out_17, decoder416_1_out_19, decoder416_1_out_20, decoder416_1_out_17);
  or hf (hf_out, hf_1_out, hf_2_out);
  or hg_1 (hg_1_out, decoder416_1_out_7, decoder416_1_out_8, decoder416_1_out_9, decoder416_1_out_10, decoder416_1_out_11, decoder416_1_out_13, decoder416_1_out_14, decoder416_1_out_15);
  or hg_2 (hg_2_out, decoder416_1_out_16, decoder416_1_out_18, decoder416_1_out_19, decoder416_1_out_20);
  or hg (hg_out, hg_1_out, hg_2_out);
  _7_Segment_Display u_7_segment_display_1 (
    .g(hg_out), .f(hf_out), .a(ha_out), .b(hb_out), .e(he_out), .d(hd_out), .c(hc_out), .dp(1'b0));
endmodule

module Seg7Switch (
  input  A0,
  input  A1,
  input  A2,
  input  A3,
  input  S
);

  wire and_1_out, and_2_out, and_3_out, and_4_out, and_5_out, and_6_out, and_7_out, dec_a_out, dec_b_out,
       dec_c1_out, dec_c2_out, dec_d_out, dec_e_out, dec_f_out, dec_g_out, decoder416_1_out_5,
       decoder416_1_out_6, decoder416_1_out_7, decoder416_1_out_8, decoder416_1_out_9, decoder416_1_out_10,
       decoder416_1_out_11, decoder416_1_out_12, decoder416_1_out_13, decoder416_1_out_14,
       decoder416_1_out_15, decoder416_1_out_16, decoder416_1_out_17, decoder416_1_out_18,
       decoder416_1_out_19, decoder416_1_out_20, dp_out, hex_a_out, hex_b_out, hex_c_out, hex_d_out,
       hex_e_out, hex_f_out, hex_g_out, mrg_a_out, mrg_b_out, mrg_c_out, mrg_d_out, mrg_e_out, mrg_f_out,
       mrg_g_out;

  Decoder416 decoder416_1 (
    .A0(A0), .A1(A1), .A2(A2), .A3(A3), .out_5(decoder416_1_out_5), .out_6(decoder416_1_out_6),
    .out_7(decoder416_1_out_7), .out_8(decoder416_1_out_8), .out_9(decoder416_1_out_9),
    .out_10(decoder416_1_out_10), .out_11(decoder416_1_out_11), .out_12(decoder416_1_out_12),
    .out_13(decoder416_1_out_13), .out_14(decoder416_1_out_14), .out_15(decoder416_1_out_15),
    .out_16(decoder416_1_out_16), .out_17(decoder416_1_out_17), .out_18(decoder416_1_out_18),
    .out_19(decoder416_1_out_19), .out_20(decoder416_1_out_20));
  and and_1 (and_1_out, S, decoder416_1_out_15);
  and and_2 (and_2_out, S, decoder416_1_out_16);
  and and_3 (and_3_out, S, decoder416_1_out_17);
  and and_4 (and_4_out, S, decoder416_1_out_18);
  and and_5 (and_5_out, S, decoder416_1_out_19);
  and and_6 (and_6_out, S, decoder416_1_out_20);
  or dec_a (dec_a_out, decoder416_1_out_5, decoder416_1_out_7, decoder416_1_out_8, decoder416_1_out_10, decoder416_1_out_11, decoder416_1_out_12, decoder416_1_out_13, decoder416_1_out_14);
  or dec_b (dec_b_out, decoder416_1_out_5, decoder416_1_out_6, decoder416_1_out_7, decoder416_1_out_8, decoder416_1_out_9, decoder416_1_out_12, decoder416_1_out_13, decoder416_1_out_14);
  or dec_c1 (dec_c1_out, decoder416_1_out_5, decoder416_1_out_6, decoder416_1_out_8, decoder416_1_out_9, decoder416_1_out_10, decoder416_1_out_11, decoder416_1_out_12, decoder416_1_out_13);
  or dec_d (dec_d_out, decoder416_1_out_5, decoder416_1_out_7, decoder416_1_out_8, decoder416_1_out_10, decoder416_1_out_11, decoder416_1_out_13, decoder416_1_out_14, decoder416_1_out_5);
  or dec_e (dec_e_out, decoder416_1_out_5, decoder416_1_out_7, decoder416_1_out_11, decoder416_1_out_13);
  or dec_f (dec_f_out, decoder416_1_out_5, decoder416_1_out_9, decoder416_1_out_10, decoder416_1_out_11, decoder416_1_out_13, decoder416_1_out_14);
  or dec_g (dec_g_out, decoder416_1_out_7, decoder416_1_out_8, decoder416_1_out_9, decoder416_1_out_10, decoder416_1_out_11, decoder416_1_out_13, decoder416_1_out_14, decoder416_1_out_7);
  or dp (dp_out, decoder416_1_out_15, decoder416_1_out_16, decoder416_1_out_17, decoder416_1_out_18, decoder416_1_out_19, decoder416_1_out_20);
  or dec_c2 (dec_c2_out, dec_c1_out, decoder416_1_out_14, dec_c1_out, dec_c1_out);
  or hex_a (hex_a_out, and_1_out, and_3_out, and_5_out, and_6_out);
  or hex_b (hex_b_out, and_1_out, and_4_out, and_1_out, and_1_out);
  or hex_c (hex_c_out, and_1_out, and_2_out, and_4_out, and_1_out);
  or hex_d (hex_d_out, and_2_out, and_3_out, and_4_out, and_5_out);
  or hex_e (hex_e_out, and_1_out, and_2_out, and_3_out, and_4_out, and_5_out, and_6_out);
  or hex_f (hex_f_out, and_1_out, and_2_out, and_3_out, and_5_out, and_6_out, and_1_out);
  or hex_g (hex_g_out, and_1_out, and_2_out, and_4_out, and_5_out, and_6_out, and_1_out);
  or mrg_a (mrg_a_out, dec_a_out, hex_a_out, dec_a_out, dec_a_out);
  or mrg_b (mrg_b_out, dec_b_out, hex_b_out, dec_b_out, dec_b_out);
  or mrg_c (mrg_c_out, dec_c2_out, hex_c_out, dec_c2_out, dec_c2_out);
  or mrg_d (mrg_d_out, dec_d_out, hex_d_out, dec_d_out, dec_d_out);
  or mrg_e (mrg_e_out, dec_e_out, hex_e_out, dec_e_out, dec_e_out);
  or mrg_f (mrg_f_out, dec_f_out, hex_f_out, dec_f_out, dec_f_out);
  or mrg_g (mrg_g_out, dec_g_out, hex_g_out, dec_g_out, dec_g_out);
  not not_1 (dp_out, S);
  and and_7 (and_7_out, dp_out, dp_out);
  _7_Segment_Display u_7_segment_display_1 (
    .g(mrg_g_out), .f(mrg_f_out), .a(mrg_a_out), .b(mrg_b_out), .e(mrg_e_out), .d(mrg_d_out), .c(mrg_c_out),
    .dp(and_7_out));
endmodule

module Seg7hex (
  input  A0,
  input  A1,
  input  A2,
  input  A3
);

  wire decoder416_1_out_5, decoder416_1_out_6, decoder416_1_out_7, decoder416_1_out_8, decoder416_1_out_9,
       decoder416_1_out_10, decoder416_1_out_11, decoder416_1_out_12, decoder416_1_out_13,
       decoder416_1_out_14, decoder416_1_out_15, decoder416_1_out_16, decoder416_1_out_17,
       decoder416_1_out_18, decoder416_1_out_19, decoder416_1_out_20, ha_1_out, ha_2_out, ha_out, hb_1_out,
       hb_2_out, hb_out, hc_1_out, hc_2_out, hc_out, hd_1_out, hd_2_out, hd_out, he_1_out, he_2_out, he_out,
       hf_1_out, hf_2_out, hf_out, hg_1_out, hg_2_out, hg_out;

  Decoder416 decoder416_1 (
    .A0(A0), .A1(A1), .A2(A2), .A3(A3), .out_5(decoder416_1_out_5), .out_6(decoder416_1_out_6),
    .out_7(decoder416_1_out_7), .out_8(decoder416_1_out_8), .out_9(decoder416_1_out_9),
    .out_10(decoder416_1_out_10), .out_11(decoder416_1_out_11), .out_12(decoder416_1_out_12),
    .out_13(decoder416_1_out_13), .out_14(decoder416_1_out_14), .out_15(decoder416_1_out_15),
    .out_16(decoder416_1_out_16), .out_17(decoder416_1_out_17), .out_18(decoder416_1_out_18),
    .out_19(decoder416_1_out_19), .out_20(decoder416_1_out_20));
  or ha_1 (ha_1_out, decoder416_1_out_5, decoder416_1_out_7, decoder416_1_out_8, decoder416_1_out_10, decoder416_1_out_11, decoder416_1_out_12, decoder416_1_out_13, decoder416_1_out_14);
  or ha_2 (ha_2_out, decoder416_1_out_15, decoder416_1_out_17, decoder416_1_out_19, decoder416_1_out_20);
  or ha (ha_out, ha_1_out, ha_2_out);
  or hb_1 (hb_1_out, decoder416_1_out_5, decoder416_1_out_6, decoder416_1_out_7, decoder416_1_out_8, decoder416_1_out_9, decoder416_1_out_12, decoder416_1_out_13, decoder416_1_out_14);
  or hb_2 (hb_2_out, decoder416_1_out_15, decoder416_1_out_18, decoder416_1_out_15, decoder416_1_out_15);
  or hb (hb_out, hb_1_out, hb_2_out);
  or hc_1 (hc_1_out, decoder416_1_out_5, decoder416_1_out_6, decoder416_1_out_8, decoder416_1_out_9, decoder416_1_out_10, decoder416_1_out_11, decoder416_1_out_12, decoder416_1_out_13);
  or hc_2 (hc_2_out, decoder416_1_out_14, decoder416_1_out_15, decoder416_1_out_16, decoder416_1_out_18);
  or hc (hc_out, hc_1_out, hc_2_out);
  or hd_1 (hd_1_out, decoder416_1_out_5, decoder416_1_out_7, decoder416_1_out_8, decoder416_1_out_10, decoder416_1_out_11, decoder416_1_out_13, decoder416_1_out_14, decoder416_1_out_16);
  or hd_2 (hd_2_out, decoder416_1_out_17, decoder416_1_out_18, decoder416_1_out_19, decoder416_1_out_17);
  or hd (hd_out, hd_1_out, hd_2_out);
  or he_1 (he_1_out, decoder416_1_out_5, decoder416_1_out_7, decoder416_1_out_11, decoder416_1_out_13, decoder416_1_out_15, decoder416_1_out_16, decoder416_1_out_17, decoder416_1_out_18);
  or he_2 (he_2_out, decoder416_1_out_19, decoder416_1_out_20, decoder416_1_out_19, decoder416_1_out_19);
  or he (he_out, he_1_out, he_2_out);
  or hf_1 (hf_1_out, decoder416_1_out_5, decoder416_1_out_9, decoder416_1_out_10, decoder416_1_out_11, decoder416_1_out_13, decoder416_1_out_14, decoder416_1_out_15, decoder416_1_out_16);
  or hf_2 (hf_2_out, decoder416_1_out_17, decoder416_1_out_19, decoder416_1_out_20, decoder416_1_out_17);
  or hf (hf_out, hf_1_out, hf_2_out);
  or hg_1 (hg_1_out, decoder416_1_out_7, decoder416_1_out_8, decoder416_1_out_9, decoder416_1_out_10, decoder416_1_out_11, decoder416_1_out_13, decoder416_1_out_14, decoder416_1_out_15);
  or hg_2 (hg_2_out, decoder416_1_out_16, decoder416_1_out_18, decoder416_1_out_19, decoder416_1_out_20);
  or hg (hg_out, hg_1_out, hg_2_out);
  _7_Segment_Display u_7_segment_display_1 (
    .g(hg_out), .f(hf_out), .a(ha_out), .b(hb_out), .e(he_out), .d(hd_out), .c(hc_out), .dp(1'b0));
endmodule

module XOR (
  input  x,
  input  y,
  output o
);

  wire And1_out, And2_out, not_1_out, not_2_out;

  not not_1 (not_1_out, y);
  not not_2 (not_2_out, x);
  and And1 (And1_out, x, not_1_out);
  and And2 (And2_out, not_2_out, y);
  or or1 (o, And1_out, And2_out);

  // Notes on the sheet:
  //   XOR
endmodule

module NOR2 (
  input  in_1,
  input  in_2,
  output out_3
);

  wire transistor_1_out, transistor_2_out, transistor_3_out, transistor_6_out;

  Transistor transistor_1 (.in(1'b1), .out(transistor_1_out), .gate(in_1));
  Transistor transistor_2 (.in(transistor_1_out), .out(transistor_2_out), .gate(in_2));
  Transistor #(.\type ("n")) transistor_3 (.in(transistor_2_out), .out(transistor_3_out), .gate(in_1));
  Transistor #(.\type ("n")) transistor_4 (.in(transistor_2_out), .out(transistor_3_out), .gate(in_2));
  Transistor transistor_5 (.in(1'b1), .out(out_3), .gate(transistor_2_out));
  Transistor #(.\type ("n")) transistor_6 (.in(out_3), .out(transistor_6_out), .gate(transistor_2_out));
  // also tied to GND on the sheet: {transistor_3_out, transistor_6_out}
endmodule

module Subtractor4BitSeg7hex (
  input  in_1,
  input  in_2,
  input  in_3,
  input  in_4,
  input  in_5,
  input  in_6,
  input  in_7,
  input  in_8
);

  wire decoder416_1_out_5, decoder416_1_out_6, decoder416_1_out_7, decoder416_1_out_8, decoder416_1_out_9,
       decoder416_1_out_10, decoder416_1_out_11, decoder416_1_out_12, decoder416_1_out_13,
       decoder416_1_out_14, decoder416_1_out_15, decoder416_1_out_16, decoder416_1_out_17,
       decoder416_1_out_18, decoder416_1_out_19, decoder416_1_out_20, fulladder_1_cout, fulladder_1_out_4,
       fulladder_2_cout, fulladder_2_out_4, fulladder_3_cout, fulladder_3_out_4, fulladder_4_cout,
       fulladder_4_out_4, ha_1_out, ha_2_out, ha_out, hb_1_out, hb_2_out, hb_out, hc_1_out, hc_2_out, hc_out,
       hd_1_out, hd_2_out, hd_out, he_1_out, he_2_out, he_out, hf_1_out, hf_2_out, hf_out, hg_1_out,
       hg_2_out, hg_out, not_1_out, not_2_out, not_3_out, not_4_out;

  not not_1 (not_1_out, in_5);
  FullAdder fulladder_1 (.in_1(in_1), .in_2(not_1_out), .Cin(1'b1), .out_4(fulladder_1_out_4), .Cout(fulladder_1_cout));
  not not_2 (not_2_out, in_6);
  FullAdder fulladder_2 (
    .in_1(in_2), .in_2(not_2_out), .Cin(fulladder_1_cout), .out_4(fulladder_2_out_4), .Cout(fulladder_2_cout));
  not not_3 (not_3_out, in_7);
  FullAdder fulladder_3 (
    .in_1(in_3), .in_2(not_3_out), .Cin(fulladder_2_cout), .out_4(fulladder_3_out_4), .Cout(fulladder_3_cout));
  not not_4 (not_4_out, in_8);
  FullAdder fulladder_4 (
    .in_1(in_4), .in_2(not_4_out), .Cin(fulladder_3_cout), .out_4(fulladder_4_out_4), .Cout(fulladder_4_cout));
  LED led_1 (.in(fulladder_4_cout));
  Decoder416 decoder416_1 (
    .A0(fulladder_1_out_4), .A1(fulladder_2_out_4), .A2(fulladder_3_out_4), .A3(fulladder_4_out_4),
    .out_5(decoder416_1_out_5), .out_6(decoder416_1_out_6), .out_7(decoder416_1_out_7),
    .out_8(decoder416_1_out_8), .out_9(decoder416_1_out_9), .out_10(decoder416_1_out_10),
    .out_11(decoder416_1_out_11), .out_12(decoder416_1_out_12), .out_13(decoder416_1_out_13),
    .out_14(decoder416_1_out_14), .out_15(decoder416_1_out_15), .out_16(decoder416_1_out_16),
    .out_17(decoder416_1_out_17), .out_18(decoder416_1_out_18), .out_19(decoder416_1_out_19),
    .out_20(decoder416_1_out_20));
  or ha_1 (ha_1_out, decoder416_1_out_5, decoder416_1_out_7, decoder416_1_out_8, decoder416_1_out_10, decoder416_1_out_11, decoder416_1_out_12, decoder416_1_out_13, decoder416_1_out_14);
  or ha_2 (ha_2_out, decoder416_1_out_15, decoder416_1_out_17, decoder416_1_out_19, decoder416_1_out_20);
  or ha (ha_out, ha_1_out, ha_2_out);
  or hb_1 (hb_1_out, decoder416_1_out_5, decoder416_1_out_6, decoder416_1_out_7, decoder416_1_out_8, decoder416_1_out_9, decoder416_1_out_12, decoder416_1_out_13, decoder416_1_out_14);
  or hb_2 (hb_2_out, decoder416_1_out_15, decoder416_1_out_18, decoder416_1_out_15, decoder416_1_out_15);
  or hb (hb_out, hb_1_out, hb_2_out);
  or hc_1 (hc_1_out, decoder416_1_out_5, decoder416_1_out_6, decoder416_1_out_8, decoder416_1_out_9, decoder416_1_out_10, decoder416_1_out_11, decoder416_1_out_12, decoder416_1_out_13);
  or hc_2 (hc_2_out, decoder416_1_out_14, decoder416_1_out_15, decoder416_1_out_16, decoder416_1_out_18);
  or hc (hc_out, hc_1_out, hc_2_out);
  or hd_1 (hd_1_out, decoder416_1_out_5, decoder416_1_out_7, decoder416_1_out_8, decoder416_1_out_10, decoder416_1_out_11, decoder416_1_out_13, decoder416_1_out_14, decoder416_1_out_16);
  or hd_2 (hd_2_out, decoder416_1_out_17, decoder416_1_out_18, decoder416_1_out_19, decoder416_1_out_17);
  or hd (hd_out, hd_1_out, hd_2_out);
  or he_1 (he_1_out, decoder416_1_out_5, decoder416_1_out_7, decoder416_1_out_11, decoder416_1_out_13, decoder416_1_out_15, decoder416_1_out_16, decoder416_1_out_17, decoder416_1_out_18);
  or he_2 (he_2_out, decoder416_1_out_19, decoder416_1_out_20, decoder416_1_out_19, decoder416_1_out_19);
  or he (he_out, he_1_out, he_2_out);
  or hf_1 (hf_1_out, decoder416_1_out_5, decoder416_1_out_9, decoder416_1_out_10, decoder416_1_out_11, decoder416_1_out_13, decoder416_1_out_14, decoder416_1_out_15, decoder416_1_out_16);
  or hf_2 (hf_2_out, decoder416_1_out_17, decoder416_1_out_19, decoder416_1_out_20, decoder416_1_out_17);
  or hf (hf_out, hf_1_out, hf_2_out);
  or hg_1 (hg_1_out, decoder416_1_out_7, decoder416_1_out_8, decoder416_1_out_9, decoder416_1_out_10, decoder416_1_out_11, decoder416_1_out_13, decoder416_1_out_14, decoder416_1_out_15);
  or hg_2 (hg_2_out, decoder416_1_out_16, decoder416_1_out_18, decoder416_1_out_19, decoder416_1_out_20);
  or hg (hg_out, hg_1_out, hg_2_out);
  _7_Segment_Display u_7_segment_display_1 (
    .g(hg_out), .f(hf_out), .a(ha_out), .b(hb_out), .e(he_out), .d(hd_out), .c(hc_out), .dp(1'b0));
endmodule

module YuanMaAdder4bit (
  input  A,
  input  B,
  input  in_3,
  input  in_4,
  input  in_5,
  input  in_6,
  input  in_7,
  input  in_8,
  input  in_9
);

  wire and_1_out, decoder416_1_out_5, decoder416_1_out_6, decoder416_1_out_7, decoder416_1_out_8,
       decoder416_1_out_9, decoder416_1_out_10, decoder416_1_out_11, decoder416_1_out_12,
       decoder416_1_out_13, decoder416_1_out_14, decoder416_1_out_15, decoder416_1_out_16,
       decoder416_1_out_17, decoder416_1_out_18, decoder416_1_out_19, decoder416_1_out_20, fulladder_1_cout,
       fulladder_1_out_4, fulladder_2_cout, fulladder_2_out_4, fulladder_3_cout, fulladder_3_out_4,
       fulladder_4_cout, fulladder_4_out_4, fulladder_5_cout, fulladder_5_out_4, fulladder_6_cout,
       fulladder_6_out_4, fulladder_7_cout, fulladder_7_out_4, fulladder_8_cout, fulladder_8_out_4,
       fulladder_9_cout, fulladder_9_out_4, ha_1_out, ha_2_out, ha_out, hb_1_out, hb_2_out, hb_out, hc_1_out,
       hc_2_out, hc_out, hd_1_out, hd_2_out, hd_out, he_1_out, he_2_out, he_out, hf_1_out, hf_2_out, hf_out,
       hg_1_out, hg_2_out, hg_out, multiplexer121_1_out_4, multiplexer121_2_out_4, multiplexer121_3_out_4,
       multiplexer121_4_out_4, multiplexer121_5_out_4, multiplexer121_6_out_4, multiplexer121_7_out_4,
       multiplexer121_8_out_4, not_1_out, not_2_out, not_3_out, not_4_out, not_5_out, not_6_out, not_7_out,
       xnor_1_out;

  not not_1 (not_1_out, in_4);
  not not_2 (not_2_out, in_8);
  FullAdder fulladder_1 (.in_1(in_8), .in_2(in_4), .Cin(in_9), .out_4(fulladder_1_out_4), .Cout(fulladder_1_cout));
  FullAdder fulladder_2 (.in_1(in_8), .in_2(not_1_out), .Cin(1'b1), .out_4(fulladder_2_out_4), .Cout(fulladder_2_cout));
  FullAdder fulladder_3 (.in_1(in_4), .in_2(not_2_out), .Cin(1'b1), .out_4(fulladder_3_out_4), .Cout(fulladder_3_cout));
  not not_3 (not_3_out, in_3);
  not not_4 (not_4_out, in_7);
  FullAdder fulladder_4 (
    .in_1(in_7), .in_2(in_3), .Cin(fulladder_1_cout), .out_4(fulladder_4_out_4), .Cout(fulladder_4_cout));
  FullAdder fulladder_5 (
    .in_1(in_7), .in_2(not_3_out), .Cin(fulladder_2_cout), .out_4(fulladder_5_out_4), .Cout(fulladder_5_cout));
  FullAdder fulladder_6 (
    .in_1(in_3), .in_2(not_4_out), .Cin(fulladder_3_cout), .out_4(fulladder_6_out_4), .Cout(fulladder_6_cout));
  xnor xnor_1 (xnor_1_out, A, in_5);
  not not_5 (not_5_out, B);
  not not_6 (not_6_out, in_6);
  FullAdder fulladder_7 (
    .in_1(in_6), .in_2(B), .Cin(fulladder_4_cout), .out_4(fulladder_7_out_4), .Cout(fulladder_7_cout));
  FullAdder fulladder_8 (
    .in_1(in_6), .in_2(not_5_out), .Cin(fulladder_5_cout), .out_4(fulladder_8_out_4), .Cout(fulladder_8_cout));
  FullAdder fulladder_9 (
    .in_1(B), .in_2(not_6_out), .Cin(fulladder_6_cout), .out_4(fulladder_9_out_4), .Cout(fulladder_9_cout));
  LED led_1 (.in(fulladder_9_cout));
  not not_7 (not_7_out, fulladder_8_cout);
  Multiplexer121 multiplexer121_1 (
    .in_1(fulladder_2_out_4), .in_2(not_7_out), .in_3(fulladder_3_out_4), .out_4(multiplexer121_1_out_4));
  Multiplexer121 multiplexer121_2 (
    .in_1(fulladder_5_out_4), .in_2(not_7_out), .in_3(fulladder_6_out_4), .out_4(multiplexer121_2_out_4));
  Multiplexer121 multiplexer121_3 (
    .in_1(fulladder_8_out_4), .in_2(not_7_out), .in_3(fulladder_9_out_4), .out_4(multiplexer121_3_out_4));
  Decoder416 decoder416_1 (
    .A0(multiplexer121_4_out_4), .A1(multiplexer121_5_out_4), .A2(multiplexer121_6_out_4), .A3(1'b0),
    .out_5(decoder416_1_out_5), .out_6(decoder416_1_out_6), .out_7(decoder416_1_out_7),
    .out_8(decoder416_1_out_8), .out_9(decoder416_1_out_9), .out_10(decoder416_1_out_10),
    .out_11(decoder416_1_out_11), .out_12(decoder416_1_out_12), .out_13(decoder416_1_out_13),
    .out_14(decoder416_1_out_14), .out_15(decoder416_1_out_15), .out_16(decoder416_1_out_16),
    .out_17(decoder416_1_out_17), .out_18(decoder416_1_out_18), .out_19(decoder416_1_out_19),
    .out_20(decoder416_1_out_20));
  and and_1 (and_1_out, xnor_1_out, fulladder_7_cout);
  Multiplexer121 multiplexer121_4 (
    .in_1(multiplexer121_1_out_4), .in_2(xnor_1_out), .in_3(fulladder_1_out_4), .out_4(multiplexer121_4_out_4));
  Multiplexer121 multiplexer121_5 (
    .in_1(multiplexer121_2_out_4), .in_2(xnor_1_out), .in_3(fulladder_4_out_4), .out_4(multiplexer121_5_out_4));
  Multiplexer121 multiplexer121_6 (
    .in_1(multiplexer121_3_out_4), .in_2(xnor_1_out), .in_3(fulladder_7_out_4), .out_4(multiplexer121_6_out_4));
  LED led_2 (.in(and_1_out));
  Multiplexer121 multiplexer121_7 (.in_1(A), .in_2(fulladder_8_cout), .in_3(in_5), .out_4(multiplexer121_7_out_4));
  Multiplexer121 multiplexer121_8 (
    .in_1(multiplexer121_7_out_4), .in_2(xnor_1_out), .in_3(in_5), .out_4(multiplexer121_8_out_4));
  or ha_1 (ha_1_out, decoder416_1_out_5, decoder416_1_out_7, decoder416_1_out_8, decoder416_1_out_10, decoder416_1_out_11, decoder416_1_out_12, decoder416_1_out_13, decoder416_1_out_14);
  or ha_2 (ha_2_out, decoder416_1_out_15, decoder416_1_out_17, decoder416_1_out_19, decoder416_1_out_20);
  or ha (ha_out, ha_1_out, ha_2_out);
  or hb_1 (hb_1_out, decoder416_1_out_5, decoder416_1_out_6, decoder416_1_out_7, decoder416_1_out_8, decoder416_1_out_9, decoder416_1_out_12, decoder416_1_out_13, decoder416_1_out_14);
  or hb_2 (hb_2_out, decoder416_1_out_15, decoder416_1_out_18, decoder416_1_out_15, decoder416_1_out_15);
  or hb (hb_out, hb_1_out, hb_2_out);
  or hc_1 (hc_1_out, decoder416_1_out_5, decoder416_1_out_6, decoder416_1_out_8, decoder416_1_out_9, decoder416_1_out_10, decoder416_1_out_11, decoder416_1_out_12, decoder416_1_out_13);
  or hc_2 (hc_2_out, decoder416_1_out_14, decoder416_1_out_15, decoder416_1_out_16, decoder416_1_out_18);
  or hc (hc_out, hc_1_out, hc_2_out);
  or hd_1 (hd_1_out, decoder416_1_out_5, decoder416_1_out_7, decoder416_1_out_8, decoder416_1_out_10, decoder416_1_out_11, decoder416_1_out_13, decoder416_1_out_14, decoder416_1_out_16);
  or hd_2 (hd_2_out, decoder416_1_out_17, decoder416_1_out_18, decoder416_1_out_19, decoder416_1_out_17);
  or hd (hd_out, hd_1_out, hd_2_out);
  or he_1 (he_1_out, decoder416_1_out_5, decoder416_1_out_7, decoder416_1_out_11, decoder416_1_out_13, decoder416_1_out_15, decoder416_1_out_16, decoder416_1_out_17, decoder416_1_out_18);
  or he_2 (he_2_out, decoder416_1_out_19, decoder416_1_out_20, decoder416_1_out_19, decoder416_1_out_19);
  or he (he_out, he_1_out, he_2_out);
  or hf_1 (hf_1_out, decoder416_1_out_5, decoder416_1_out_9, decoder416_1_out_10, decoder416_1_out_11, decoder416_1_out_13, decoder416_1_out_14, decoder416_1_out_15, decoder416_1_out_16);
  or hf_2 (hf_2_out, decoder416_1_out_17, decoder416_1_out_19, decoder416_1_out_20, decoder416_1_out_17);
  or hf (hf_out, hf_1_out, hf_2_out);
  or hg_1 (hg_1_out, decoder416_1_out_7, decoder416_1_out_8, decoder416_1_out_9, decoder416_1_out_10, decoder416_1_out_11, decoder416_1_out_13, decoder416_1_out_14, decoder416_1_out_15);
  or hg_2 (hg_2_out, decoder416_1_out_16, decoder416_1_out_18, decoder416_1_out_19, decoder416_1_out_20);
  or hg (hg_out, hg_1_out, hg_2_out);
  _7_Segment_Display u_7_segment_display_1 (
    .g(multiplexer121_8_out_4), .f(1'b0), .a(1'b0), .b(1'b0), .e(1'b0), .d(1'b0), .c(1'b0), .dp(1'b0));
  _7_Segment_Display u_7_segment_display_2 (
    .g(hg_out), .f(hf_out), .a(ha_out), .b(hb_out), .e(he_out), .d(hd_out), .c(hc_out), .dp(1'b0));

  // Notes on the sheet:
  //   A+B
  //   A-B
  //   B-A
endmodule

module FanMaAdder4bit (
  input  in_1,
  input  A,
  input  in_3,
  input  in_4,
  input  in_5,
  input  B,
  input  in_7,
  input  in_8
);

  wire decoder416_1_out_5, decoder416_1_out_6, decoder416_1_out_7, decoder416_1_out_8, decoder416_1_out_9,
       decoder416_1_out_10, decoder416_1_out_11, decoder416_1_out_12, decoder416_1_out_13,
       decoder416_1_out_14, decoder416_1_out_15, decoder416_1_out_16, decoder416_1_out_17,
       decoder416_1_out_18, decoder416_1_out_19, decoder416_1_out_20, fulladder_1_cout, fulladder_1_out_4,
       fulladder_2_cout, fulladder_2_out_4, fulladder_3_cout, fulladder_3_out_4, fulladder_4_cout,
       fulladder_4_out_4, ha_1_out, ha_2_out, ha_out, hb_1_out, hb_2_out, hb_out, hc_1_out, hc_2_out, hc_out,
       hd_1_out, hd_2_out, hd_out, he_1_out, he_2_out, he_out, hf_1_out, hf_2_out, hf_out, hg_1_out,
       hg_2_out, hg_out;

  FullAdder fulladder_1 (
    .in_1(in_4), .in_2(in_8), .Cin(fulladder_4_cout), .out_4(fulladder_1_out_4), .Cout(fulladder_1_cout));
  FullAdder fulladder_2 (
    .in_1(in_3), .in_2(in_7), .Cin(fulladder_1_cout), .out_4(fulladder_2_out_4), .Cout(fulladder_2_cout));
  FullAdder fulladder_3 (
    .in_1(A), .in_2(B), .Cin(fulladder_2_cout), .out_4(fulladder_3_out_4), .Cout(fulladder_3_cout));
  FullAdder fulladder_4 (
    .in_1(in_1), .in_2(in_5), .Cin(fulladder_3_cout), .out_4(fulladder_4_out_4), .Cout(fulladder_4_cout));
  Decoder416 decoder416_1 (
    .A0(fulladder_1_out_4), .A1(fulladder_2_out_4), .A2(fulladder_3_out_4), .A3(fulladder_4_out_4),
    .out_5(decoder416_1_out_5), .out_6(decoder416_1_out_6), .out_7(decoder416_1_out_7),
    .out_8(decoder416_1_out_8), .out_9(decoder416_1_out_9), .out_10(decoder416_1_out_10),
    .out_11(decoder416_1_out_11), .out_12(decoder416_1_out_12), .out_13(decoder416_1_out_13),
    .out_14(decoder416_1_out_14), .out_15(decoder416_1_out_15), .out_16(decoder416_1_out_16),
    .out_17(decoder416_1_out_17), .out_18(decoder416_1_out_18), .out_19(decoder416_1_out_19),
    .out_20(decoder416_1_out_20));
  or ha_1 (ha_1_out, decoder416_1_out_5, decoder416_1_out_7, decoder416_1_out_8, decoder416_1_out_10, decoder416_1_out_11, decoder416_1_out_12, decoder416_1_out_13, decoder416_1_out_14);
  or ha_2 (ha_2_out, decoder416_1_out_15, decoder416_1_out_17, decoder416_1_out_19, decoder416_1_out_20);
  or ha (ha_out, ha_1_out, ha_2_out);
  or hb_1 (hb_1_out, decoder416_1_out_5, decoder416_1_out_6, decoder416_1_out_7, decoder416_1_out_8, decoder416_1_out_9, decoder416_1_out_12, decoder416_1_out_13, decoder416_1_out_14);
  or hb_2 (hb_2_out, decoder416_1_out_15, decoder416_1_out_18, decoder416_1_out_15, decoder416_1_out_15);
  or hb (hb_out, hb_1_out, hb_2_out);
  or hc_1 (hc_1_out, decoder416_1_out_5, decoder416_1_out_6, decoder416_1_out_8, decoder416_1_out_9, decoder416_1_out_10, decoder416_1_out_11, decoder416_1_out_12, decoder416_1_out_13);
  or hc_2 (hc_2_out, decoder416_1_out_14, decoder416_1_out_15, decoder416_1_out_16, decoder416_1_out_18);
  or hc (hc_out, hc_1_out, hc_2_out);
  or hd_1 (hd_1_out, decoder416_1_out_5, decoder416_1_out_7, decoder416_1_out_8, decoder416_1_out_10, decoder416_1_out_11, decoder416_1_out_13, decoder416_1_out_14, decoder416_1_out_16);
  or hd_2 (hd_2_out, decoder416_1_out_17, decoder416_1_out_18, decoder416_1_out_19, decoder416_1_out_17);
  or hd (hd_out, hd_1_out, hd_2_out);
  or he_1 (he_1_out, decoder416_1_out_5, decoder416_1_out_7, decoder416_1_out_11, decoder416_1_out_13, decoder416_1_out_15, decoder416_1_out_16, decoder416_1_out_17, decoder416_1_out_18);
  or he_2 (he_2_out, decoder416_1_out_19, decoder416_1_out_20, decoder416_1_out_19, decoder416_1_out_19);
  or he (he_out, he_1_out, he_2_out);
  or hf_1 (hf_1_out, decoder416_1_out_5, decoder416_1_out_9, decoder416_1_out_10, decoder416_1_out_11, decoder416_1_out_13, decoder416_1_out_14, decoder416_1_out_15, decoder416_1_out_16);
  or hf_2 (hf_2_out, decoder416_1_out_17, decoder416_1_out_19, decoder416_1_out_20, decoder416_1_out_17);
  or hf (hf_out, hf_1_out, hf_2_out);
  or hg_1 (hg_1_out, decoder416_1_out_7, decoder416_1_out_8, decoder416_1_out_9, decoder416_1_out_10, decoder416_1_out_11, decoder416_1_out_13, decoder416_1_out_14, decoder416_1_out_15);
  or hg_2 (hg_2_out, decoder416_1_out_16, decoder416_1_out_18, decoder416_1_out_19, decoder416_1_out_20);
  or hg (hg_out, hg_1_out, hg_2_out);
  _7_Segment_Display u_7_segment_display_1 (
    .g(hg_out), .f(hf_out), .a(ha_out), .b(hb_out), .e(he_out), .d(hd_out), .c(hc_out), .dp(1'b0));
endmodule

module Adder4bitOverflowJudge (
  input  in_1,
  input  A,
  input  in_3,
  input  in_4,
  input  in_5,
  input  B,
  input  in_7,
  input  in_8
);

  wire fulladder_1_cout, fulladder_2_cout, fulladder_3_cout, fulladder_4_cout, xor_1_o;

  FullAdder fulladder_1 (.in_1(in_4), .in_2(in_8), .Cin(1'b0), .Cout(fulladder_1_cout));  // open: out_4
  FullAdder fulladder_2 (.in_1(in_3), .in_2(in_7), .Cin(fulladder_1_cout), .Cout(fulladder_2_cout));  // open: out_4
  FullAdder fulladder_3 (.in_1(A), .in_2(B), .Cin(fulladder_2_cout), .Cout(fulladder_3_cout));  // open: out_4
  FullAdder fulladder_4 (.in_1(in_1), .in_2(in_5), .Cin(fulladder_3_cout), .Cout(fulladder_4_cout));  // open: out_4
  XOR xor_1 (.x(fulladder_3_cout), .y(fulladder_4_cout), .o(xor_1_o));
  LED led_1 (.in(xor_1_o));
endmodule

module SRLatchMetastability (
  input  R,
  input  in_2,
  input  S,
  output Q,
  output minus_Q
);

  wire and_1_out, and_2_out;

  and and_1 (and_1_out, R, in_2);
  and and_2 (and_2_out, in_2, S);
  nor nor_1 (Q, and_1_out, minus_Q);
  nor nor_2 (minus_Q, Q, and_2_out);
endmodule

module DLatch (
  input  D,
  input  WE,
  output Q,
  output minus_Q
);

  wire and_1_out, and_2_out, not_1_out;

  not not_1 (not_1_out, D);
  and and_1 (and_1_out, D, WE);
  and and_2 (and_2_out, WE, not_1_out);
  SRLatch srlatch_1 (.R(and_2_out), .S(and_1_out), .Q(Q), .minus_Q(minus_Q));
endmodule

module SRLatch (
  input  R,
  input  S,
  output Q,
  output minus_Q
);

  nor nor_1 (Q, R, minus_Q);
  nor nor_2 (minus_Q, Q, S);
endmodule

module DLatchReset (
  input  WE,
  input  D,
  input  Reset,
  output Q,
  output minus_Q
);

  wire and_1_out, and_2_out, not_1_out, or_1_out;

  not not_1 (not_1_out, D);
  and and_1 (and_1_out, D, WE);
  and and_2 (and_2_out, WE, not_1_out);
  or or_1 (or_1_out, and_2_out, Reset);
  SRLatch srlatch_1 (.R(or_1_out), .S(and_1_out), .Q(Q), .minus_Q(minus_Q));
endmodule

module DLatchResetFlip (
  input  in_1,
  output out_2
);

  wire dlatchreset_1_minus_q;

  DLatchReset dlatchreset_1 (
    .WE(dlatchreset_1_minus_q), .D(dlatchreset_1_minus_q), .Reset(in_1), .Q(out_2),
    .minus_Q(dlatchreset_1_minus_q));
  // also tied to VCC on the sheet: dlatchreset_1_minus_q
endmodule

module DFlipFlop (
  input  in_1,
  output out_2
);

  wire button_1_out, dlatch_1_q, not_1_out;

  Button button_1 (.out(button_1_out));
  not not_1 (not_1_out, button_1_out);
  DLatch dlatch_1 (.D(not_1_out), .WE(in_1), .Q(dlatch_1_q));  // open: minus_Q
  DLatch dlatch_2 (.D(button_1_out), .WE(dlatch_1_q), .Q(out_2));  // open: minus_Q

  // Notes on the sheet:
  //   上we 下D
endmodule

module DFlipFlopReset (
  input  CLK,
  input  in_2,
  input  in_3,
  output out_4
);

  wire dlatchreset_1_q, not_1_out;

  not not_1 (not_1_out, CLK);
  DLatchReset dlatchreset_1 (.WE(not_1_out), .D(in_2), .Reset(in_3), .Q(dlatchreset_1_q));  // open: minus_Q
  DLatchReset dlatchreset_2 (.WE(CLK), .D(dlatchreset_1_q), .Reset(in_3), .Q(out_4));  // open: minus_Q

  // Notes on the sheet:
  //   上we 下D
endmodule

module DFlipFlopResetFlip (
  input  in_1,
  output out_2
);

  wire button_1_out, not_1_out;

  Button button_1 (.out(button_1_out));
  not not_1 (not_1_out, out_2);
  DFlipFlopReset dflipflopreset_1 (.CLK(button_1_out), .in_2(not_1_out), .in_3(in_1), .out_4(out_2));
endmodule

module DFlipFlopEnReset (
  input  CLK,
  input  EN,
  input  in_3,
  input  in_4,
  output out_5
);

  wire dlatchreset_1_q, multiplexer121_1_out_4, not_1_out;

  Multiplexer121 multiplexer121_1 (.in_1(out_5), .in_2(EN), .in_3(in_3), .out_4(multiplexer121_1_out_4));
  not not_1 (not_1_out, CLK);
  DLatchReset dlatchreset_1 (
    .WE(not_1_out), .D(multiplexer121_1_out_4), .Reset(in_4), .Q(dlatchreset_1_q));  // open: minus_Q
  DLatchReset dlatchreset_2 (.WE(CLK), .D(dlatchreset_1_q), .Reset(in_4), .Q(out_5));  // open: minus_Q

  // Notes on the sheet:
  //   上we 下D
endmodule

module Register4Bit (
  input  EN,
  input  in_2,
  input  Reset,
  input  in_4,
  input  in_5,
  input  in_6
);

  wire button_1_out, decoder416_1_out_5, decoder416_1_out_6, decoder416_1_out_7, decoder416_1_out_8,
       decoder416_1_out_9, decoder416_1_out_10, decoder416_1_out_11, decoder416_1_out_12,
       decoder416_1_out_13, decoder416_1_out_14, decoder416_1_out_15, decoder416_1_out_16,
       decoder416_1_out_17, decoder416_1_out_18, decoder416_1_out_19, decoder416_1_out_20,
       dflipflopenreset_1_out_5, dflipflopenreset_2_out_5, dflipflopenreset_3_out_5,
       dflipflopenreset_4_out_5, ha_1_out, ha_2_out, ha_out, hb_1_out, hb_2_out, hb_out, hc_1_out, hc_2_out,
       hc_out, hd_1_out, hd_2_out, hd_out, he_1_out, he_2_out, he_out, hf_1_out, hf_2_out, hf_out, hg_1_out,
       hg_2_out, hg_out;

  Button button_1 (.out(button_1_out));
  DFlipFlopEnReset dflipflopenreset_1 (
    .CLK(button_1_out), .EN(EN), .in_3(in_2), .in_4(Reset), .out_5(dflipflopenreset_1_out_5));
  DFlipFlopEnReset dflipflopenreset_2 (
    .CLK(button_1_out), .EN(EN), .in_3(in_4), .in_4(Reset), .out_5(dflipflopenreset_2_out_5));
  DFlipFlopEnReset dflipflopenreset_3 (
    .CLK(button_1_out), .EN(EN), .in_3(in_5), .in_4(Reset), .out_5(dflipflopenreset_3_out_5));
  DFlipFlopEnReset dflipflopenreset_4 (
    .CLK(button_1_out), .EN(EN), .in_3(in_6), .in_4(Reset), .out_5(dflipflopenreset_4_out_5));
  Decoder416 decoder416_1 (
    .A0(dflipflopenreset_1_out_5), .A1(dflipflopenreset_2_out_5), .A2(dflipflopenreset_3_out_5),
    .A3(dflipflopenreset_4_out_5), .out_5(decoder416_1_out_5), .out_6(decoder416_1_out_6),
    .out_7(decoder416_1_out_7), .out_8(decoder416_1_out_8), .out_9(decoder416_1_out_9),
    .out_10(decoder416_1_out_10), .out_11(decoder416_1_out_11), .out_12(decoder416_1_out_12),
    .out_13(decoder416_1_out_13), .out_14(decoder416_1_out_14), .out_15(decoder416_1_out_15),
    .out_16(decoder416_1_out_16), .out_17(decoder416_1_out_17), .out_18(decoder416_1_out_18),
    .out_19(decoder416_1_out_19), .out_20(decoder416_1_out_20));
  or ha_1 (ha_1_out, decoder416_1_out_5, decoder416_1_out_7, decoder416_1_out_8, decoder416_1_out_10, decoder416_1_out_11, decoder416_1_out_12, decoder416_1_out_13, decoder416_1_out_14);
  or ha_2 (ha_2_out, decoder416_1_out_15, decoder416_1_out_17, decoder416_1_out_19, decoder416_1_out_20);
  or ha (ha_out, ha_1_out, ha_2_out);
  or hb_1 (hb_1_out, decoder416_1_out_5, decoder416_1_out_6, decoder416_1_out_7, decoder416_1_out_8, decoder416_1_out_9, decoder416_1_out_12, decoder416_1_out_13, decoder416_1_out_14);
  or hb_2 (hb_2_out, decoder416_1_out_15, decoder416_1_out_18, decoder416_1_out_15, decoder416_1_out_15);
  or hb (hb_out, hb_1_out, hb_2_out);
  or hc_1 (hc_1_out, decoder416_1_out_5, decoder416_1_out_6, decoder416_1_out_8, decoder416_1_out_9, decoder416_1_out_10, decoder416_1_out_11, decoder416_1_out_12, decoder416_1_out_13);
  or hc_2 (hc_2_out, decoder416_1_out_14, decoder416_1_out_15, decoder416_1_out_16, decoder416_1_out_18);
  or hc (hc_out, hc_1_out, hc_2_out);
  or hd_1 (hd_1_out, decoder416_1_out_5, decoder416_1_out_7, decoder416_1_out_8, decoder416_1_out_10, decoder416_1_out_11, decoder416_1_out_13, decoder416_1_out_14, decoder416_1_out_16);
  or hd_2 (hd_2_out, decoder416_1_out_17, decoder416_1_out_18, decoder416_1_out_19, decoder416_1_out_17);
  or hd (hd_out, hd_1_out, hd_2_out);
  or he_1 (he_1_out, decoder416_1_out_5, decoder416_1_out_7, decoder416_1_out_11, decoder416_1_out_13, decoder416_1_out_15, decoder416_1_out_16, decoder416_1_out_17, decoder416_1_out_18);
  or he_2 (he_2_out, decoder416_1_out_19, decoder416_1_out_20, decoder416_1_out_19, decoder416_1_out_19);
  or he (he_out, he_1_out, he_2_out);
  or hf_1 (hf_1_out, decoder416_1_out_5, decoder416_1_out_9, decoder416_1_out_10, decoder416_1_out_11, decoder416_1_out_13, decoder416_1_out_14, decoder416_1_out_15, decoder416_1_out_16);
  or hf_2 (hf_2_out, decoder416_1_out_17, decoder416_1_out_19, decoder416_1_out_20, decoder416_1_out_17);
  or hf (hf_out, hf_1_out, hf_2_out);
  or hg_1 (hg_1_out, decoder416_1_out_7, decoder416_1_out_8, decoder416_1_out_9, decoder416_1_out_10, decoder416_1_out_11, decoder416_1_out_13, decoder416_1_out_14, decoder416_1_out_15);
  or hg_2 (hg_2_out, decoder416_1_out_16, decoder416_1_out_18, decoder416_1_out_19, decoder416_1_out_20);
  or hg (hg_out, hg_1_out, hg_2_out);
  _7_Segment_Display u_7_segment_display_1 (
    .g(hg_out), .f(hf_out), .a(ha_out), .b(hb_out), .e(he_out), .d(hd_out), .c(hc_out), .dp(1'b0));
endmodule

module Counter4Bit (
  input  in_1,
  input  in_2,
  input  in_3,
  input  in_4,
  input  EN,
  input  Reset
);

  wire button_1_out, fulladder_1_cout, fulladder_1_out_4, fulladder_2_cout, fulladder_2_out_4,
       fulladder_3_cout, fulladder_3_out_4, fulladder_4_out_4;
  wire [3:0] dflipflopenreset_1_out_5;

  FullAdder fulladder_1 (
    .in_1(dflipflopenreset_1_out_5[0]), .in_2(in_4), .Cin(1'b0), .out_4(fulladder_1_out_4),
    .Cout(fulladder_1_cout));
  FullAdder fulladder_2 (
    .in_1(dflipflopenreset_1_out_5[1]), .in_2(in_3), .Cin(fulladder_1_cout), .out_4(fulladder_2_out_4),
    .Cout(fulladder_2_cout));
  Button button_1 (.out(button_1_out));
  FullAdder fulladder_3 (
    .in_1(dflipflopenreset_1_out_5[2]), .in_2(in_2), .Cin(fulladder_2_cout), .out_4(fulladder_3_out_4),
    .Cout(fulladder_3_cout));
  DFlipFlopEnReset dflipflopenreset_1 (
    .CLK(button_1_out), .EN(EN), .in_3(fulladder_1_out_4), .in_4(Reset), .out_5(dflipflopenreset_1_out_5[0]));
  DFlipFlopEnReset dflipflopenreset_2 (
    .CLK(button_1_out), .EN(EN), .in_3(fulladder_2_out_4), .in_4(Reset), .out_5(dflipflopenreset_1_out_5[1]));
  DFlipFlopEnReset dflipflopenreset_3 (
    .CLK(button_1_out), .EN(EN), .in_3(fulladder_3_out_4), .in_4(Reset), .out_5(dflipflopenreset_1_out_5[2]));
  DFlipFlopEnReset dflipflopenreset_4 (
    .CLK(button_1_out), .EN(EN), .in_3(fulladder_4_out_4), .in_4(Reset), .out_5(dflipflopenreset_1_out_5[3]));
  FullAdder fulladder_4 (
    .in_1(dflipflopenreset_1_out_5[3]), .in_2(in_1), .Cin(fulladder_3_cout), .out_4(fulladder_4_out_4));  // open: Cout
  Hex_Digit_Display hex_digit_display_1 (.value(dflipflopenreset_1_out_5));  // open: dp
endmodule

module Sum1to10 (
  input  in_1,
  input  in_2,
  input  in_3,
  input  Reset
);

  wire and_1_out, button_1_out, decoder416_1_out_5, decoder416_1_out_6, decoder416_1_out_7,
       decoder416_1_out_8, decoder416_1_out_9, decoder416_1_out_10, decoder416_1_out_11, decoder416_1_out_12,
       decoder416_1_out_13, decoder416_1_out_14, decoder416_1_out_15, decoder416_1_out_16,
       decoder416_1_out_17, decoder416_1_out_18, decoder416_1_out_19, decoder416_1_out_20,
       decoder416_2_out_5, decoder416_2_out_6, decoder416_2_out_7, decoder416_2_out_8, decoder416_2_out_9,
       decoder416_2_out_10, decoder416_2_out_11, decoder416_2_out_12, decoder416_2_out_13,
       decoder416_2_out_14, decoder416_2_out_15, decoder416_2_out_16, decoder416_2_out_17,
       decoder416_2_out_18, decoder416_2_out_19, decoder416_2_out_20, dflipflopenreset_1_out_5,
       dflipflopenreset_2_out_5, dflipflopenreset_3_out_5, dflipflopenreset_4_out_5,
       dflipflopenreset_5_out_5, dflipflopenreset_6_out_5, dflipflopenreset_7_out_5,
       dflipflopenreset_8_out_5, dflipflopenreset_9_out_5, dflipflopenreset_10_out_5,
       dflipflopenreset_11_out_5, dflipflopenreset_12_out_5, fulladder_1_cout, fulladder_1_out_4,
       fulladder_2_cout, fulladder_2_out_4, fulladder_3_cout, fulladder_3_out_4, fulladder_4_cout,
       fulladder_4_out_4, fulladder_5_cout, fulladder_5_out_4, fulladder_6_cout, fulladder_6_out_4,
       fulladder_7_out_4, fulladder_8_cout, fulladder_8_out_4, fulladder_9_cout, fulladder_9_out_4,
       fulladder_10_cout, fulladder_10_out_4, fulladder_11_cout, fulladder_11_out_4, fulladder_12_out_4,
       ha_1_out, ha_2_out, ha_out, hb_1_out, hb_2_out, hb_out, hc_1_out, hc_2_out, hc_out, hd_1_out,
       hd_2_out, hd_out, he_1_out, he_2_out, he_out, hf_1_out, hf_2_out, hf_out, hg_1_out, hg_2_out, hg_out,
       not_1_out, not_2_out, or_1_out, or_2_out, or_3_out, or_4_out, or_5_out, or_6_out, or_7_out, or_8_out,
       or_9_out, or_10_out, or_11_out, or_12_out, or_13_out, or_14_out, or_15_out, or_16_out, or_17_out,
       or_18_out, or_19_out, or_20_out, or_21_out;

  Button button_1 (.out(button_1_out));
  FullAdder fulladder_1 (
    .in_1(dflipflopenreset_1_out_5), .in_2(1'b1), .Cin(1'b0), .out_4(fulladder_1_out_4),
    .Cout(fulladder_1_cout));
  FullAdder fulladder_2 (
    .in_1(dflipflopenreset_5_out_5), .in_2(dflipflopenreset_1_out_5), .Cin(1'b0), .out_4(fulladder_2_out_4),
    .Cout(fulladder_2_cout));
  FullAdder fulladder_3 (
    .in_1(dflipflopenreset_2_out_5), .in_2(in_3), .Cin(fulladder_1_cout), .out_4(fulladder_3_out_4),
    .Cout(fulladder_3_cout));
  FullAdder fulladder_4 (
    .in_1(dflipflopenreset_6_out_5), .in_2(dflipflopenreset_2_out_5), .Cin(fulladder_2_cout),
    .out_4(fulladder_4_out_4), .Cout(fulladder_4_cout));
  FullAdder fulladder_5 (
    .in_1(dflipflopenreset_3_out_5), .in_2(in_2), .Cin(fulladder_3_cout), .out_4(fulladder_5_out_4),
    .Cout(fulladder_5_cout));
  FullAdder fulladder_6 (
    .in_1(dflipflopenreset_7_out_5), .in_2(dflipflopenreset_3_out_5), .Cin(fulladder_4_cout),
    .out_4(fulladder_6_out_4), .Cout(fulladder_6_cout));
  DFlipFlopEnReset dflipflopenreset_1 (
    .CLK(button_1_out), .EN(not_2_out), .in_3(fulladder_1_out_4), .in_4(Reset),
    .out_5(dflipflopenreset_1_out_5));
  DFlipFlopEnReset dflipflopenreset_2 (
    .CLK(button_1_out), .EN(not_2_out), .in_3(fulladder_3_out_4), .in_4(Reset),
    .out_5(dflipflopenreset_2_out_5));
  DFlipFlopEnReset dflipflopenreset_3 (
    .CLK(button_1_out), .EN(not_2_out), .in_3(fulladder_5_out_4), .in_4(Reset),
    .out_5(dflipflopenreset_3_out_5));
  DFlipFlopEnReset dflipflopenreset_4 (
    .CLK(button_1_out), .EN(not_2_out), .in_3(fulladder_7_out_4), .in_4(Reset),
    .out_5(dflipflopenreset_4_out_5));
  FullAdder fulladder_7 (
    .in_1(dflipflopenreset_4_out_5), .in_2(in_1), .Cin(fulladder_5_cout), .out_4(fulladder_7_out_4));  // open: Cout
  FullAdder fulladder_8 (
    .in_1(dflipflopenreset_8_out_5), .in_2(dflipflopenreset_4_out_5), .Cin(fulladder_6_cout),
    .out_4(fulladder_8_out_4), .Cout(fulladder_8_cout));
  DFlipFlopEnReset dflipflopenreset_5 (
    .CLK(button_1_out), .EN(not_2_out), .in_3(fulladder_2_out_4), .in_4(Reset),
    .out_5(dflipflopenreset_5_out_5));
  DFlipFlopEnReset dflipflopenreset_6 (
    .CLK(button_1_out), .EN(not_2_out), .in_3(fulladder_4_out_4), .in_4(Reset),
    .out_5(dflipflopenreset_6_out_5));
  DFlipFlopEnReset dflipflopenreset_7 (
    .CLK(button_1_out), .EN(not_2_out), .in_3(fulladder_6_out_4), .in_4(Reset),
    .out_5(dflipflopenreset_7_out_5));
  DFlipFlopEnReset dflipflopenreset_8 (
    .CLK(button_1_out), .EN(not_2_out), .in_3(fulladder_8_out_4), .in_4(Reset),
    .out_5(dflipflopenreset_8_out_5));
  DFlipFlopEnReset dflipflopenreset_9 (
    .CLK(button_1_out), .EN(not_2_out), .in_3(fulladder_9_out_4), .in_4(Reset),
    .out_5(dflipflopenreset_9_out_5));
  DFlipFlopEnReset dflipflopenreset_10 (
    .CLK(button_1_out), .EN(not_2_out), .in_3(fulladder_10_out_4), .in_4(Reset),
    .out_5(dflipflopenreset_10_out_5));
  DFlipFlopEnReset dflipflopenreset_11 (
    .CLK(button_1_out), .EN(not_2_out), .in_3(fulladder_11_out_4), .in_4(Reset),
    .out_5(dflipflopenreset_11_out_5));
  DFlipFlopEnReset dflipflopenreset_12 (
    .CLK(button_1_out), .EN(not_2_out), .in_3(fulladder_12_out_4), .in_4(Reset),
    .out_5(dflipflopenreset_12_out_5));
  not not_1 (not_1_out, dflipflopenreset_3_out_5);
  FullAdder fulladder_9 (
    .in_1(dflipflopenreset_9_out_5), .in_2(1'b0), .Cin(fulladder_8_cout), .out_4(fulladder_9_out_4),
    .Cout(fulladder_9_cout));
  and and_1 (and_1_out, dflipflopenreset_1_out_5, dflipflopenreset_2_out_5, not_1_out, dflipflopenreset_4_out_5);
  FullAdder fulladder_10 (
    .in_1(dflipflopenreset_10_out_5), .in_2(1'b0), .Cin(fulladder_9_cout), .out_4(fulladder_10_out_4),
    .Cout(fulladder_10_cout));
  not not_2 (not_2_out, and_1_out);
  FullAdder fulladder_11 (
    .in_1(dflipflopenreset_11_out_5), .in_2(1'b0), .Cin(fulladder_10_cout), .out_4(fulladder_11_out_4),
    .Cout(fulladder_11_cout));
  FullAdder fulladder_12 (
    .in_1(dflipflopenreset_12_out_5), .in_2(1'b0), .Cin(fulladder_11_cout), .out_4(fulladder_12_out_4));  // open: Cout
  Decoder416 decoder416_1 (
    .A0(dflipflopenreset_5_out_5), .A1(dflipflopenreset_6_out_5), .A2(dflipflopenreset_7_out_5),
    .A3(dflipflopenreset_8_out_5), .out_5(decoder416_1_out_5), .out_6(decoder416_1_out_6),
    .out_7(decoder416_1_out_7), .out_8(decoder416_1_out_8), .out_9(decoder416_1_out_9),
    .out_10(decoder416_1_out_10), .out_11(decoder416_1_out_11), .out_12(decoder416_1_out_12),
    .out_13(decoder416_1_out_13), .out_14(decoder416_1_out_14), .out_15(decoder416_1_out_15),
    .out_16(decoder416_1_out_16), .out_17(decoder416_1_out_17), .out_18(decoder416_1_out_18),
    .out_19(decoder416_1_out_19), .out_20(decoder416_1_out_20));
  Decoder416 decoder416_2 (
    .A0(dflipflopenreset_9_out_5), .A1(dflipflopenreset_10_out_5), .A2(dflipflopenreset_11_out_5),
    .A3(dflipflopenreset_12_out_5), .out_5(decoder416_2_out_5), .out_6(decoder416_2_out_6),
    .out_7(decoder416_2_out_7), .out_8(decoder416_2_out_8), .out_9(decoder416_2_out_9),
    .out_10(decoder416_2_out_10), .out_11(decoder416_2_out_11), .out_12(decoder416_2_out_12),
    .out_13(decoder416_2_out_13), .out_14(decoder416_2_out_14), .out_15(decoder416_2_out_15),
    .out_16(decoder416_2_out_16), .out_17(decoder416_2_out_17), .out_18(decoder416_2_out_18),
    .out_19(decoder416_2_out_19), .out_20(decoder416_2_out_20));
  or ha_1 (ha_1_out, decoder416_1_out_5, decoder416_1_out_7, decoder416_1_out_8, decoder416_1_out_10, decoder416_1_out_11, decoder416_1_out_12, decoder416_1_out_13, decoder416_1_out_14);
  or ha_2 (ha_2_out, decoder416_1_out_15, decoder416_1_out_17, decoder416_1_out_19, decoder416_1_out_20);
  or ha (ha_out, ha_1_out, ha_2_out);
  or hb_1 (hb_1_out, decoder416_1_out_5, decoder416_1_out_6, decoder416_1_out_7, decoder416_1_out_8, decoder416_1_out_9, decoder416_1_out_12, decoder416_1_out_13, decoder416_1_out_14);
  or hb_2 (hb_2_out, decoder416_1_out_15, decoder416_1_out_18, decoder416_1_out_15, decoder416_1_out_15);
  or hb (hb_out, hb_1_out, hb_2_out);
  or hc_1 (hc_1_out, decoder416_1_out_5, decoder416_1_out_6, decoder416_1_out_8, decoder416_1_out_9, decoder416_1_out_10, decoder416_1_out_11, decoder416_1_out_12, decoder416_1_out_13);
  or hc_2 (hc_2_out, decoder416_1_out_14, decoder416_1_out_15, decoder416_1_out_16, decoder416_1_out_18);
  or hc (hc_out, hc_1_out, hc_2_out);
  or hd_1 (hd_1_out, decoder416_1_out_5, decoder416_1_out_7, decoder416_1_out_8, decoder416_1_out_10, decoder416_1_out_11, decoder416_1_out_13, decoder416_1_out_14, decoder416_1_out_16);
  or hd_2 (hd_2_out, decoder416_1_out_17, decoder416_1_out_18, decoder416_1_out_19, decoder416_1_out_17);
  or hd (hd_out, hd_1_out, hd_2_out);
  or he_1 (he_1_out, decoder416_1_out_5, decoder416_1_out_7, decoder416_1_out_11, decoder416_1_out_13, decoder416_1_out_15, decoder416_1_out_16, decoder416_1_out_17, decoder416_1_out_18);
  or he_2 (he_2_out, decoder416_1_out_19, decoder416_1_out_20, decoder416_1_out_19, decoder416_1_out_19);
  or he (he_out, he_1_out, he_2_out);
  or hf_1 (hf_1_out, decoder416_1_out_5, decoder416_1_out_9, decoder416_1_out_10, decoder416_1_out_11, decoder416_1_out_13, decoder416_1_out_14, decoder416_1_out_15, decoder416_1_out_16);
  or hf_2 (hf_2_out, decoder416_1_out_17, decoder416_1_out_19, decoder416_1_out_20, decoder416_1_out_17);
  or hf (hf_out, hf_1_out, hf_2_out);
  or hg_1 (hg_1_out, decoder416_1_out_7, decoder416_1_out_8, decoder416_1_out_9, decoder416_1_out_10, decoder416_1_out_11, decoder416_1_out_13, decoder416_1_out_14, decoder416_1_out_15);
  or hg_2 (hg_2_out, decoder416_1_out_16, decoder416_1_out_18, decoder416_1_out_19, decoder416_1_out_20);
  or hg (hg_out, hg_1_out, hg_2_out);
  or or_1 (or_1_out, decoder416_2_out_5, decoder416_2_out_7, decoder416_2_out_8, decoder416_2_out_10, decoder416_2_out_11, decoder416_2_out_12, decoder416_2_out_13, decoder416_2_out_14);
  or or_2 (or_2_out, decoder416_2_out_15, decoder416_2_out_17, decoder416_2_out_19, decoder416_2_out_20);
  or or_3 (or_3_out, or_1_out, or_2_out);
  or or_4 (or_4_out, decoder416_2_out_5, decoder416_2_out_6, decoder416_2_out_7, decoder416_2_out_8, decoder416_2_out_9, decoder416_2_out_12, decoder416_2_out_13, decoder416_2_out_14);
  or or_5 (or_5_out, decoder416_2_out_15, decoder416_2_out_18, decoder416_2_out_15, decoder416_2_out_15);
  or or_6 (or_6_out, or_4_out, or_5_out);
  or or_7 (or_7_out, decoder416_2_out_5, decoder416_2_out_6, decoder416_2_out_8, decoder416_2_out_9, decoder416_2_out_10, decoder416_2_out_11, decoder416_2_out_12, decoder416_2_out_13);
  or or_8 (or_8_out, decoder416_2_out_14, decoder416_2_out_15, decoder416_2_out_16, decoder416_2_out_18);
  or or_9 (or_9_out, or_7_out, or_8_out);
  or or_10 (or_10_out, decoder416_2_out_5, decoder416_2_out_7, decoder416_2_out_8, decoder416_2_out_10, decoder416_2_out_11, decoder416_2_out_13, decoder416_2_out_14, decoder416_2_out_16);
  or or_11 (or_11_out, decoder416_2_out_17, decoder416_2_out_18, decoder416_2_out_19, decoder416_2_out_17);
  or or_12 (or_12_out, or_10_out, or_11_out);
  or or_13 (or_13_out, decoder416_2_out_5, decoder416_2_out_7, decoder416_2_out_11, decoder416_2_out_13, decoder416_2_out_15, decoder416_2_out_16, decoder416_2_out_17, decoder416_2_out_18);
  or or_14 (or_14_out, decoder416_2_out_19, decoder416_2_out_20, decoder416_2_out_19, decoder416_2_out_19);
  or or_15 (or_15_out, or_13_out, or_14_out);
  or or_16 (or_16_out, decoder416_2_out_5, decoder416_2_out_9, decoder416_2_out_10, decoder416_2_out_11, decoder416_2_out_13, decoder416_2_out_14, decoder416_2_out_15, decoder416_2_out_16);
  or or_17 (or_17_out, decoder416_2_out_17, decoder416_2_out_19, decoder416_2_out_20, decoder416_2_out_17);
  or or_18 (or_18_out, or_16_out, or_17_out);
  or or_19 (or_19_out, decoder416_2_out_7, decoder416_2_out_8, decoder416_2_out_9, decoder416_2_out_10, decoder416_2_out_11, decoder416_2_out_13, decoder416_2_out_14, decoder416_2_out_15);
  or or_20 (or_20_out, decoder416_2_out_16, decoder416_2_out_18, decoder416_2_out_19, decoder416_2_out_20);
  or or_21 (or_21_out, or_19_out, or_20_out);
  _7_Segment_Display u_7_segment_display_1 (
    .g(or_21_out), .f(or_18_out), .a(or_3_out), .b(or_6_out), .e(or_15_out), .d(or_12_out), .c(or_9_out),
    .dp(1'b0));
  _7_Segment_Display u_7_segment_display_2 (
    .g(hg_out), .f(hf_out), .a(ha_out), .b(hb_out), .e(he_out), .d(hd_out), .c(hc_out), .dp(1'b0));

  // Notes on the sheet:
  //   EN
  //   EN
  //   Reset
  //   低位
  //   高位
endmodule

module Digit9 (
  input  CLK,
  input  EN,
  input  Reset,
  output out_4,
  output out_5,
  output out_6,
  output out_7,
  output carry
);

  wire and_1_out, and_2_out, and_3_out, and_4_out, fulladder_1_cout, fulladder_1_out_4, fulladder_2_cout,
       fulladder_2_out_4, fulladder_3_cout, fulladder_3_out_4, fulladder_4_out_4, not_1_out, not_2_out,
       not_3_out;

  FullAdder fulladder_1 (.in_1(out_4), .in_2(1'b1), .Cin(1'b0), .out_4(fulladder_1_out_4), .Cout(fulladder_1_cout));
  and and_1 (and_1_out, fulladder_1_out_4, not_3_out);
  and and_2 (and_2_out, fulladder_2_out_4, not_3_out);
  and and_3 (and_3_out, fulladder_3_out_4, not_3_out);
  and and_4 (and_4_out, fulladder_4_out_4, not_3_out);
  FullAdder fulladder_2 (
    .in_1(out_5), .in_2(1'b0), .Cin(fulladder_1_cout), .out_4(fulladder_2_out_4), .Cout(fulladder_2_cout));
  FullAdder fulladder_3 (
    .in_1(out_6), .in_2(1'b0), .Cin(fulladder_2_cout), .out_4(fulladder_3_out_4), .Cout(fulladder_3_cout));
  DFlipFlopEnReset dflipflopenreset_1 (.CLK(CLK), .EN(EN), .in_3(and_1_out), .in_4(Reset), .out_5(out_4));
  DFlipFlopEnReset dflipflopenreset_2 (.CLK(CLK), .EN(EN), .in_3(and_2_out), .in_4(Reset), .out_5(out_5));
  DFlipFlopEnReset dflipflopenreset_3 (.CLK(CLK), .EN(EN), .in_3(and_3_out), .in_4(Reset), .out_5(out_6));
  DFlipFlopEnReset dflipflopenreset_4 (.CLK(CLK), .EN(EN), .in_3(and_4_out), .in_4(Reset), .out_5(out_7));
  FullAdder fulladder_4 (.in_1(out_7), .in_2(1'b0), .Cin(fulladder_3_cout), .out_4(fulladder_4_out_4));  // open: Cout
  not not_1 (not_1_out, out_5);
  not not_2 (not_2_out, out_6);
  and and_5 (carry, out_4, not_1_out, not_2_out, out_7);
  not not_3 (not_3_out, carry);
endmodule

module Digit5 (
  input  CLK,
  input  EN,
  input  Reset,
  output out_4,
  output out_5,
  output out_6,
  output out_7,
  output carry
);

  wire and_1_out, and_2_out, and_3_out, and_4_out, fulladder_1_cout, fulladder_1_out_4, fulladder_2_cout,
       fulladder_2_out_4, fulladder_3_cout, fulladder_3_out_4, fulladder_4_out_4, not_1_out, not_2_out,
       not_3_out;

  FullAdder fulladder_1 (.in_1(out_4), .in_2(1'b1), .Cin(1'b0), .out_4(fulladder_1_out_4), .Cout(fulladder_1_cout));
  and and_1 (and_1_out, fulladder_1_out_4, not_3_out);
  and and_2 (and_2_out, fulladder_2_out_4, not_3_out);
  and and_3 (and_3_out, fulladder_3_out_4, not_3_out);
  and and_4 (and_4_out, fulladder_4_out_4, not_3_out);
  FullAdder fulladder_2 (
    .in_1(out_5), .in_2(1'b0), .Cin(fulladder_1_cout), .out_4(fulladder_2_out_4), .Cout(fulladder_2_cout));
  FullAdder fulladder_3 (
    .in_1(out_6), .in_2(1'b0), .Cin(fulladder_2_cout), .out_4(fulladder_3_out_4), .Cout(fulladder_3_cout));
  DFlipFlopEnReset dflipflopenreset_1 (.CLK(CLK), .EN(EN), .in_3(and_1_out), .in_4(Reset), .out_5(out_4));
  DFlipFlopEnReset dflipflopenreset_2 (.CLK(CLK), .EN(EN), .in_3(and_2_out), .in_4(Reset), .out_5(out_5));
  DFlipFlopEnReset dflipflopenreset_3 (.CLK(CLK), .EN(EN), .in_3(and_3_out), .in_4(Reset), .out_5(out_6));
  DFlipFlopEnReset dflipflopenreset_4 (.CLK(CLK), .EN(EN), .in_3(and_4_out), .in_4(Reset), .out_5(out_7));
  FullAdder fulladder_4 (.in_1(out_7), .in_2(1'b0), .Cin(fulladder_3_cout), .out_4(fulladder_4_out_4));  // open: Cout
  not not_1 (not_1_out, out_5);
  not not_2 (not_2_out, out_7);
  and and_5 (carry, out_4, not_1_out, out_6, not_2_out);
  not not_3 (not_3_out, carry);
endmodule

module EClock (
  input  Reset
);

  wire and_1_out, and_2_out, clock_1_out, digit5_1_carry, digit9_1_carry, digit9_2_carry;
  wire [3:0] digit5_1_out_4, digit5_2_out_4, digit9_1_out_4, digit9_2_out_4;

  Clock clock_1 (.out(clock_1_out));
  Digit9 digit9_1 (
    .CLK(clock_1_out), .EN(1'b1), .Reset(Reset), .out_4(digit9_1_out_4[0]), .out_5(digit9_1_out_4[1]),
    .out_6(digit9_1_out_4[2]), .out_7(digit9_1_out_4[3]), .carry(digit9_1_carry));
  Digit5 digit5_1 (
    .CLK(clock_1_out), .EN(digit9_1_carry), .Reset(Reset), .out_4(digit5_1_out_4[0]),
    .out_5(digit5_1_out_4[1]), .out_6(digit5_1_out_4[2]), .out_7(digit5_1_out_4[3]), .carry(digit5_1_carry));
  Digit9 digit9_2 (
    .CLK(clock_1_out), .EN(and_1_out), .Reset(Reset), .out_4(digit9_2_out_4[0]), .out_5(digit9_2_out_4[1]),
    .out_6(digit9_2_out_4[2]), .out_7(digit9_2_out_4[3]), .carry(digit9_2_carry));
  Digit5 digit5_2 (
    .CLK(clock_1_out), .EN(and_2_out), .Reset(Reset), .out_4(digit5_2_out_4[0]), .out_5(digit5_2_out_4[1]),
    .out_6(digit5_2_out_4[2]), .out_7(digit5_2_out_4[3]));  // open: carry
  and and_1 (and_1_out, digit5_1_carry, digit9_1_carry);
  and and_2 (and_2_out, digit9_2_carry, and_1_out);
  Hex_Digit_Display hex_digit_display_1 (.value(digit5_2_out_4));  // open: dp
  Hex_Digit_Display hex_digit_display_2 (.value(digit9_2_out_4));  // open: dp
  Hex_Digit_Display hex_digit_display_3 (.value(digit5_1_out_4));  // open: dp
  Hex_Digit_Display hex_digit_display_4 (.value(digit9_1_out_4));  // open: dp
endmodule

module SumRom (
  input  [2:0] in_1,
  output [7:0] out_2
);

  Multiplexer #(.select(3), .width(8)) multiplexer_1 (
    .in0(8'h8a), .in1(8'h90), .in2(8'ha0), .in3(8'hb1), .in4(8'h17), .in5(8'h29), .in6(8'hd1), .in7(8'hdf),
    .out(out_2), .sel(in_1));
endmodule

module Fetch (
  input  clk,
  input  Reset,
  output [7:0] out_3
);

  wire fulladder_1_cout, fulladder_1_out_4, fulladder_2_cout, fulladder_2_out_4, fulladder_3_out_4;
  wire [2:0] dflipflopenreset_1_out_5;

  FullAdder fulladder_1 (
    .in_1(dflipflopenreset_1_out_5[0]), .in_2(1'b1), .Cin(1'b0), .out_4(fulladder_1_out_4),
    .Cout(fulladder_1_cout));
  FullAdder fulladder_2 (
    .in_1(dflipflopenreset_1_out_5[1]), .in_2(1'b0), .Cin(fulladder_1_cout), .out_4(fulladder_2_out_4),
    .Cout(fulladder_2_cout));
  FullAdder fulladder_3 (
    .in_1(dflipflopenreset_1_out_5[2]), .in_2(1'b0), .Cin(fulladder_2_cout), .out_4(fulladder_3_out_4));  // open: Cout
  DFlipFlopEnReset dflipflopenreset_1 (
    .CLK(clk), .EN(1'b1), .in_3(fulladder_1_out_4), .in_4(Reset), .out_5(dflipflopenreset_1_out_5[0]));
  DFlipFlopEnReset dflipflopenreset_2 (
    .CLK(clk), .EN(1'b1), .in_3(fulladder_2_out_4), .in_4(Reset), .out_5(dflipflopenreset_1_out_5[1]));
  DFlipFlopEnReset dflipflopenreset_3 (
    .CLK(clk), .EN(1'b1), .in_3(fulladder_3_out_4), .in_4(Reset), .out_5(dflipflopenreset_1_out_5[2]));
  SumRom sumrom_1 (.in_1(dflipflopenreset_1_out_5), .out_2(out_3));
  Hex_Digit_Display hex_digit_display_1 (.value(out_3[7:4]));  // open: dp
  Hex_Digit_Display hex_digit_display_2 (.value(out_3[3:0]));  // open: dp

  // Notes on the sheet:
  //   EN
endmodule

module Reg8 (
  input  EN,
  input  in_2,
  input  Reset,
  input  [7:0] in_4,
  output [7:0] out_5
);

  DFlipFlopEnReset dflipflopenreset_1 (.CLK(EN), .EN(in_2), .in_3(in_4[0]), .in_4(Reset), .out_5(out_5[0]));
  DFlipFlopEnReset dflipflopenreset_2 (.CLK(EN), .EN(in_2), .in_3(in_4[1]), .in_4(Reset), .out_5(out_5[1]));
  DFlipFlopEnReset dflipflopenreset_3 (.CLK(EN), .EN(in_2), .in_3(in_4[2]), .in_4(Reset), .out_5(out_5[2]));
  DFlipFlopEnReset dflipflopenreset_4 (.CLK(EN), .EN(in_2), .in_3(in_4[3]), .in_4(Reset), .out_5(out_5[3]));
  DFlipFlopEnReset dflipflopenreset_5 (.CLK(EN), .EN(in_2), .in_3(in_4[4]), .in_4(Reset), .out_5(out_5[4]));
  DFlipFlopEnReset dflipflopenreset_6 (.CLK(EN), .EN(in_2), .in_3(in_4[5]), .in_4(Reset), .out_5(out_5[5]));
  DFlipFlopEnReset dflipflopenreset_7 (.CLK(EN), .EN(in_2), .in_3(in_4[6]), .in_4(Reset), .out_5(out_5[6]));
  DFlipFlopEnReset dflipflopenreset_8 (.CLK(EN), .EN(in_2), .in_3(in_4[7]), .in_4(Reset), .out_5(out_5[7]));
endmodule

module GPR (
  input  clk,
  input  [1:0] rd,
  input  rst,
  input  we,
  input  [7:0] wd,
  input  [1:0] rs1,
  input  [1:0] rs2,
  output [7:0] rd1,
  output [7:0] rd2
);

  wire and_1_out, and_2_out, and_3_out, and_4_out, decoder24_1_y0, decoder24_1_y1, decoder24_1_y2,
       decoder24_1_y3;
  wire [7:0] reg8_1_out_5, reg8_2_out_5, reg8_3_out_5, reg8_4_out_5;

  Decoder24 decoder24_1 (
    ._1(rd[0]), ._2(rd[1]), .en(1'b1), .Y0(decoder24_1_y0), .Y1(decoder24_1_y1), .Y2(decoder24_1_y2),
    .Y3(decoder24_1_y3));
  and and_1 (and_1_out, decoder24_1_y0, we);
  and and_2 (and_2_out, decoder24_1_y1, we);
  and and_3 (and_3_out, decoder24_1_y2, we);
  and and_4 (and_4_out, decoder24_1_y3, we);
  Reg8 reg8_1 (.EN(clk), .in_2(and_1_out), .Reset(rst), .in_4(wd), .out_5(reg8_1_out_5));
  Reg8 reg8_2 (.EN(clk), .in_2(and_2_out), .Reset(rst), .in_4(wd), .out_5(reg8_2_out_5));
  Reg8 reg8_3 (.EN(clk), .in_2(and_3_out), .Reset(rst), .in_4(wd), .out_5(reg8_3_out_5));
  Reg8 reg8_4 (.EN(clk), .in_2(and_4_out), .Reset(rst), .in_4(wd), .out_5(reg8_4_out_5));
  Multiplexer #(.select(2), .width(8)) multiplexer_1 (
    .in0(reg8_1_out_5), .in1(reg8_2_out_5), .in2(reg8_3_out_5), .in3(reg8_4_out_5), .out(rd1), .sel(rs1));
  Multiplexer #(.select(2), .width(8)) multiplexer_2 (
    .in0(reg8_1_out_5), .in1(reg8_2_out_5), .in2(reg8_3_out_5), .in3(reg8_4_out_5), .out(rd2), .sel(rs2));
endmodule

module Scpu (
  input  clk,
  input  rst,
  input  [1:0] rs1,
  output [7:0] out_4
);

  wire [7:0] bit_extender_1_out, fetch_1_out_3;

  Fetch fetch_1 (.clk(clk), .Reset(rst), .out_3(fetch_1_out_3));
  GPR gpr_1 (
    .clk(clk), .rd(fetch_1_out_3[5:4]), .rst(rst), .we(1'b1), .wd(bit_extender_1_out), .rs1(rs1),
    .rs2(2'b00), .rd1(out_4));  // open: rd2
  assign bit_extender_1_out = {{4{1'b0}}, fetch_1_out_3[3:0]};  // Bit_Extender bit_extender_1

  // Notes on the sheet:
  //   rs2
endmodule
