// Logisim project F3-nor2-or2.circ as structural Verilog: 2 circuits, main circuit main
module main (
  input  A,
  input  B,
  output out_3
);

  wire transistor_1_out, transistor_2_out;

  Transistor transistor_1 (.in(1'b1), .out(transistor_1_out), .gate(A));
  Transistor transistor_2 (.in(transistor_1_out), .out(transistor_2_out), .gate(B));
  Transistor #(.\type ("n")) transistor_3 (.in(1'b0), .out(transistor_2_out), .gate(A));
  Transistor #(.\type ("n")) transistor_4 (.in(1'b0), .out(transistor_2_out), .gate(B));
  Transistor transistor_5 (.in(1'b1), .out(out_3), .gate(transistor_2_out));
  Transistor #(.\type ("n")) transistor_6 (.in(1'b0), .out(out_3), .gate(transistor_2_out));
endmodule

module OR2 (
  input  A,
  input  B,
  output Y
);

  wire transistor_1_out, transistor_2_out;

  Transistor transistor_1 (.in(1'b1), .out(transistor_1_out), .gate(A));
  Transistor transistor_2 (.in(transistor_1_out), .out(transistor_2_out), .gate(B));
  Transistor #(.\type ("n")) transistor_3 (.in(1'b0), .out(transistor_2_out), .gate(A));
  Transistor #(.\type ("n")) transistor_4 (.in(1'b0), .out(transistor_2_out), .gate(B));
  Transistor transistor_5 (.in(1'b1), .out(Y), .gate(transistor_2_out));
  Transistor #(.\type ("n")) transistor_6 (.in(1'b0), .out(Y), .gate(transistor_2_out));
endmodule
